// Logisim project Cofre.circ as structural Verilog
module Registrador_de_Estado (
  input  CLK,
  input  N3,
  input  N2,
  input  N1,
  input  N0,
  output S3,
  output S2,
  output S1,
  output S0
);

  D_Flip_Flop d_ff_1 (.clk(CLK), .D(N3), .Q(S3));  // open: Qn, preset, en, reset
  D_Flip_Flop d_ff_2 (.clk(CLK), .D(N2), .Q(S2));  // open: Qn, preset, en, reset
  D_Flip_Flop d_ff_3 (.clk(CLK), .D(N1), .Q(S1));  // open: Qn, preset, en, reset
  D_Flip_Flop d_ff_4 (.clk(CLK), .D(N0), .Q(S0));  // open: Qn, preset, en, reset
endmodule

module Contador_20s (
  input  CLK,
  input  CLR,
  output C0,
  output C1,
  output C2,
  output C3,
  output C4
);

  wire and_1_out, and_2_out, and_3_out, ENABLE_out, pull_resistor_1_node;

  Pull_Resistor #(.pull(1)) pull_resistor_1 (.node(pull_resistor_1_node));
  J_K_Flip_Flop j_k_ff_1 (
    .J(pull_resistor_1_node), .clk(CLK), .K(pull_resistor_1_node), .Q(C0), .en(ENABLE_out), .reset(CLR));  // open: Qn, preset
  nand ENABLE (ENABLE_out, C2, C4);
  J_K_Flip_Flop j_k_ff_2 (.J(C0), .clk(CLK), .K(C0), .Q(C1), .en(ENABLE_out), .reset(CLR));  // open: Qn, preset
  and and_1 (and_1_out, C0, C1);
  J_K_Flip_Flop j_k_ff_3 (
    .J(and_1_out), .clk(CLK), .K(and_1_out), .Q(C2), .en(ENABLE_out), .reset(CLR));  // open: Qn, preset
  and and_2 (and_2_out, and_1_out, C2);
  J_K_Flip_Flop j_k_ff_4 (
    .J(and_2_out), .clk(CLK), .K(and_2_out), .Q(C3), .en(ENABLE_out), .reset(CLR));  // open: Qn, preset
  and and_3 (and_3_out, and_2_out, C3);
  J_K_Flip_Flop j_k_ff_5 (
    .J(and_3_out), .clk(CLK), .K(and_3_out), .Q(C4), .en(ENABLE_out), .reset(CLR));  // open: Qn, preset
endmodule

module N0 (
  input  S3,
  input  S2,
  input  S1,
  input  S0,
  input  COMPS,
  input  COMPT5,
  input  COMPT20,
  input  ON,
  input  ADD,
  output N0
);

  wire and_1_out, and_2_out, and_3_out, and_4_out, and_5_out, and_6_out, and_7_out, and_8_out, and_9_out,
       and_10_out, and_11_out, and_12_out, and_13_out, and_14_out, and_15_out, and_16_out, and_17_out,
       nand_1_out, not_1_out, not_2_out, not_3_out, not_4_out, not_5_out, not_6_out, not_7_out, not_8_out,
       not_9_out, not_10_out, not_11_out, not_12_out, not_13_out, not_14_out, not_15_out, not_16_out,
       not_17_out, not_18_out, not_19_out, not_20_out, not_21_out, not_22_out, not_23_out, not_24_out,
       not_25_out, not_26_out, not_27_out, not_28_out, not_29_out, not_30_out, not_31_out, not_32_out,
       not_33_out, not_34_out, not_35_out, not_36_out, or_1_out, or_2_out, or_3_out;

  not not_1 (not_1_out, ADD);
  not not_2 (not_2_out, ON);
  not not_3 (not_3_out, ON);
  not not_4 (not_4_out, ADD);
  not not_5 (not_5_out, ADD);
  not not_6 (not_6_out, ON);
  and and_1 (and_1_out, ON, not_1_out);
  and and_2 (and_2_out, not_2_out, ADD);
  and and_3 (and_3_out, not_3_out, ADD);
  and and_4 (and_4_out, ON, not_4_out);
  and and_5 (and_5_out, ON, not_5_out);
  and and_6 (and_6_out, not_6_out, ADD);
  not not_7 (not_7_out, ON);
  not not_8 (not_8_out, ADD);
  not not_9 (not_9_out, COMPT5);
  not not_10 (not_10_out, ADD);
  nand nand_1 (nand_1_out, S3, S2, S1, S0);
  not not_11 (not_11_out, S3);
  not not_12 (not_12_out, S2);
  not not_13 (not_13_out, S1);
  not not_14 (not_14_out, COMPT5);
  not not_15 (not_15_out, S3);
  not not_16 (not_16_out, S2);
  not not_17 (not_17_out, S0);
  or or_1 (or_1_out, and_1_out, and_2_out);
  not not_18 (not_18_out, S3);
  not not_19 (not_19_out, S2);
  not not_20 (not_20_out, COMPT5);
  not not_21 (not_21_out, S3);
  not not_22 (not_22_out, S1);
  not not_23 (not_23_out, S0);
  or or_2 (or_2_out, and_3_out, and_4_out);
  not not_24 (not_24_out, S3);
  not not_25 (not_25_out, S1);
  not not_26 (not_26_out, COMPT5);
  not not_27 (not_27_out, S3);
  not not_28 (not_28_out, S0);
  or or_3 (or_3_out, and_5_out, and_6_out);
  not not_29 (not_29_out, S3);
  not not_30 (not_30_out, COMPT5);
  not not_31 (not_31_out, S2);
  not not_32 (not_32_out, S1);
  not not_33 (not_33_out, S0);
  not not_34 (not_34_out, S2);
  not not_35 (not_35_out, S1);
  not not_36 (not_36_out, COMPT20);
  and and_7 (and_7_out, ON, not_10_out, nand_1_out);
  and and_8 (and_8_out, not_11_out, not_12_out, not_13_out, S0, not_14_out);
  and and_9 (and_9_out, not_15_out, not_16_out, S1, not_17_out, or_1_out);
  and and_10 (and_10_out, not_18_out, not_19_out, S1, S0, not_20_out);
  and and_11 (and_11_out, not_21_out, S2, not_22_out, not_23_out, or_2_out);
  and and_12 (and_12_out, not_24_out, S2, not_25_out, S0, not_26_out);
  and and_13 (and_13_out, not_27_out, S2, S1, not_28_out, or_3_out);
  and and_14 (and_14_out, not_29_out, S2, S1, S0, not_30_out);
  and and_15 (and_15_out, S3, not_31_out, not_32_out, not_33_out, COMPS);
  and and_16 (and_16_out, S3, not_34_out, not_35_out, S0, not_36_out);
  and and_17 (and_17_out, S3, S2, S1, S0, not_7_out, not_8_out, not_9_out);
  or or_4 (N0, and_7_out, and_8_out, and_9_out, and_10_out, and_11_out, and_12_out, and_13_out, and_14_out, and_15_out, and_16_out, and_17_out);
endmodule

module N1 (
  input  S3,
  input  S2,
  input  S1,
  input  S0,
  input  COMPS,
  input  COMPT5,
  input  COMPT20,
  input  ON,
  input  ADD,
  output N1
);

  wire and_1_out, and_2_out, and_3_out, and_4_out, and_5_out, and_6_out, and_7_out, and_8_out, and_9_out,
       and_10_out, and_11_out, and_12_out, and_13_out, and_14_out, and_15_out, and_16_out, and_17_out,
       and_18_out, and_19_out, and_20_out, and_21_out, not_1_out, not_2_out, not_3_out, not_4_out, not_5_out,
       not_6_out, not_7_out, not_8_out, not_9_out, not_10_out, not_11_out, not_12_out, not_13_out,
       not_14_out, not_15_out, not_16_out, not_17_out, not_18_out, not_19_out, not_20_out, not_21_out,
       not_22_out, not_23_out, not_24_out, not_25_out, not_26_out, not_27_out, not_28_out, not_29_out,
       not_30_out, not_31_out, not_32_out, not_33_out, not_34_out, not_35_out, not_36_out, not_37_out,
       not_38_out, or_1_out, or_2_out, or_3_out;

  not not_1 (not_1_out, ON);
  not not_2 (not_2_out, ADD);
  not not_3 (not_3_out, ADD);
  not not_4 (not_4_out, ON);
  not not_5 (not_5_out, ADD);
  not not_6 (not_6_out, ON);
  not not_7 (not_7_out, ON);
  not not_8 (not_8_out, ADD);
  not not_9 (not_9_out, ON);
  not not_10 (not_10_out, ADD);
  and and_1 (and_1_out, not_1_out, not_2_out);
  and and_2 (and_2_out, ON, ADD);
  and and_3 (and_3_out, ON, not_3_out);
  and and_4 (and_4_out, not_4_out, ADD);
  and and_5 (and_5_out, ON, not_5_out);
  and and_6 (and_6_out, not_6_out, ADD);
  and and_7 (and_7_out, not_7_out, not_8_out);
  and and_8 (and_8_out, ON, ADD);
  and and_9 (and_9_out, not_9_out, ADD);
  and and_10 (and_10_out, ON, not_10_out);
  and and_11 (and_11_out, ON, ADD);
  not not_11 (not_11_out, S3);
  not not_12 (not_12_out, S2);
  not not_13 (not_13_out, S1);
  not not_14 (not_14_out, S3);
  not not_15 (not_15_out, S2);
  not not_16 (not_16_out, S0);
  or or_1 (or_1_out, and_1_out, and_2_out, and_3_out, and_4_out);
  not not_17 (not_17_out, S3);
  not not_18 (not_18_out, S2);
  not not_19 (not_19_out, COMPT5);
  not not_20 (not_20_out, S3);
  not not_21 (not_21_out, S1);
  not not_22 (not_22_out, S0);
  not not_23 (not_23_out, ADD);
  not not_24 (not_24_out, S3);
  not not_25 (not_25_out, S1);
  not not_26 (not_26_out, ON);
  not not_27 (not_27_out, ADD);
  not not_28 (not_28_out, S3);
  not not_29 (not_29_out, S0);
  or or_2 (or_2_out, and_5_out, and_6_out, and_7_out, and_8_out);
  not not_30 (not_30_out, S3);
  not not_31 (not_31_out, COMPT5);
  not not_32 (not_32_out, S2);
  not not_33 (not_33_out, S1);
  not not_34 (not_34_out, S2);
  not not_35 (not_35_out, S0);
  or or_3 (or_3_out, and_9_out, and_10_out, and_11_out);
  not not_36 (not_36_out, ON);
  not not_37 (not_37_out, ADD);
  not not_38 (not_38_out, COMPT5);
  and and_12 (and_12_out, not_11_out, not_12_out, not_13_out, S0, COMPT5);
  and and_13 (and_13_out, not_14_out, not_15_out, S1, not_16_out, or_1_out);
  and and_14 (and_14_out, not_17_out, not_18_out, S1, S0, not_19_out);
  and and_15 (and_15_out, not_20_out, S2, not_21_out, not_22_out, ON, not_23_out);
  and and_16 (and_16_out, not_24_out, S2, not_25_out, S0, COMPT5, not_26_out, not_27_out);
  and and_17 (and_17_out, not_28_out, S2, S1, not_29_out, or_2_out);
  and and_18 (and_18_out, not_30_out, S2, S1, S0, not_31_out);
  and and_19 (and_19_out, S3, not_32_out, not_33_out, S0, COMPT20);
  and and_20 (and_20_out, S3, not_34_out, S1, not_35_out, or_3_out);
  and and_21 (and_21_out, S3, S2, S1, S0, not_36_out, not_37_out, not_38_out);
  or or_4 (N1, and_12_out, and_13_out, and_14_out, and_15_out, and_16_out, and_17_out, and_18_out, and_19_out, and_20_out, and_21_out);
endmodule

module N2 (
  input  S3,
  input  S2,
  input  S1,
  input  S0,
  input  COMPS,
  input  COMPT5,
  input  COMPT20,
  input  ON,
  input  ADD,
  output N2
);

  wire and_1_out, and_2_out, and_3_out, and_4_out, and_5_out, and_6_out, and_7_out, and_8_out, and_9_out,
       and_10_out, and_11_out, and_12_out, and_13_out, and_14_out, and_15_out, not_1_out, not_2_out,
       not_3_out, not_4_out, not_5_out, not_6_out, not_7_out, not_8_out, not_9_out, not_10_out, not_11_out,
       not_12_out, not_13_out, not_14_out, not_15_out, not_16_out, not_17_out, not_18_out, not_19_out,
       not_20_out, not_21_out, not_22_out, not_23_out, not_24_out, not_25_out, not_26_out, not_27_out,
       not_28_out, not_29_out, or_1_out, or_2_out, or_3_out;

  not not_1 (not_1_out, ADD);
  not not_2 (not_2_out, ON);
  not not_3 (not_3_out, ADD);
  not not_4 (not_4_out, ON);
  not not_5 (not_5_out, ADD);
  not not_6 (not_6_out, ON);
  not not_7 (not_7_out, ON);
  not not_8 (not_8_out, ADD);
  and and_1 (and_1_out, not_1_out, not_2_out);
  and and_2 (and_2_out, ADD, ON);
  and and_3 (and_3_out, ON, not_3_out);
  and and_4 (and_4_out, not_4_out, ADD);
  not not_9 (not_9_out, COMPT5);
  and and_5 (and_5_out, ON, not_5_out);
  and and_6 (and_6_out, not_6_out, ADD);
  and and_7 (and_7_out, not_7_out, not_8_out);
  and and_8 (and_8_out, ON, ADD);
  not not_10 (not_10_out, S3);
  not not_11 (not_11_out, S2);
  not not_12 (not_12_out, S0);
  not not_13 (not_13_out, ADD);
  not not_14 (not_14_out, S3);
  not not_15 (not_15_out, S2);
  not not_16 (not_16_out, ADD);
  not not_17 (not_17_out, ON);
  not not_18 (not_18_out, S3);
  not not_19 (not_19_out, S1);
  not not_20 (not_20_out, S0);
  or or_1 (or_1_out, and_1_out, and_2_out, and_3_out, and_4_out);
  not not_21 (not_21_out, S3);
  not not_22 (not_22_out, S1);
  or or_2 (or_2_out, not_9_out, COMPT5);
  not not_23 (not_23_out, S3);
  not not_24 (not_24_out, S0);
  or or_3 (or_3_out, and_5_out, and_6_out, and_7_out, and_8_out);
  not not_25 (not_25_out, S3);
  not not_26 (not_26_out, COMPT5);
  not not_27 (not_27_out, ON);
  not not_28 (not_28_out, ADD);
  not not_29 (not_29_out, COMPT5);
  and and_9 (and_9_out, not_10_out, not_11_out, S1, not_12_out, ON, not_13_out);
  and and_10 (and_10_out, not_14_out, not_15_out, S1, S0, COMPT5, not_16_out, not_17_out);
  and and_11 (and_11_out, not_18_out, S2, not_19_out, not_20_out, or_1_out);
  and and_12 (and_12_out, not_21_out, S2, not_22_out, S0, or_2_out);
  and and_13 (and_13_out, not_23_out, S2, S1, not_24_out, or_3_out);
  and and_14 (and_14_out, not_25_out, S2, S1, S0, not_26_out);
  and and_15 (and_15_out, S3, S2, S1, S0, not_27_out, not_28_out, not_29_out);
  or or_4 (N2, and_9_out, and_10_out, and_11_out, and_12_out, and_13_out, and_14_out, and_15_out);
endmodule

module N3 (
  input  S3,
  input  S2,
  input  S1,
  input  S0,
  input  COMPS,
  input  COMPT5,
  input  COMPT20,
  input  ON,
  input  ADD,
  output N3
);

  wire and_1_out, and_2_out, and_3_out, and_4_out, and_5_out, and_6_out, and_7_out, and_8_out, and_9_out,
       and_10_out, and_11_out, not_1_out, not_2_out, not_3_out, not_4_out, not_5_out, not_6_out, not_7_out,
       not_8_out, not_9_out, not_10_out, not_11_out, not_12_out, not_13_out, not_14_out, not_15_out,
       not_16_out, not_17_out, not_18_out, not_19_out, not_20_out, not_21_out, not_22_out, not_23_out,
       not_24_out, not_25_out, not_26_out, not_27_out, or_1_out, or_2_out;

  not not_1 (not_1_out, ON);
  not not_2 (not_2_out, ADD);
  not not_3 (not_3_out, S3);
  not not_4 (not_4_out, S2);
  not not_5 (not_5_out, S0);
  not not_6 (not_6_out, ADD);
  not not_7 (not_7_out, S3);
  not not_8 (not_8_out, S1);
  not not_9 (not_9_out, S0);
  not not_10 (not_10_out, ADD);
  not not_11 (not_11_out, S3);
  not not_12 (not_12_out, S0);
  not not_13 (not_13_out, ADD);
  not not_14 (not_14_out, S3);
  not not_15 (not_15_out, ON);
  not not_16 (not_16_out, ADD);
  not not_17 (not_17_out, COMPT20);
  and and_1 (and_1_out, not_1_out, ADD);
  and and_2 (and_2_out, ON, not_2_out);
  and and_3 (and_3_out, ON, ADD);
  not not_18 (not_18_out, ON);
  not not_19 (not_19_out, ADD);
  not not_20 (not_20_out, COMPT5);
  not not_21 (not_21_out, S2);
  not not_22 (not_22_out, S1);
  not not_23 (not_23_out, S0);
  not not_24 (not_24_out, S2);
  not not_25 (not_25_out, S1);
  or or_1 (or_1_out, not_17_out, COMPT20);
  not not_26 (not_26_out, S2);
  not not_27 (not_27_out, S0);
  or or_2 (or_2_out, and_1_out, and_2_out, and_3_out);
  and and_4 (and_4_out, not_3_out, not_4_out, S1, not_5_out, ON, not_6_out);
  and and_5 (and_5_out, not_7_out, S2, not_8_out, not_9_out, ON, not_10_out);
  and and_6 (and_6_out, not_11_out, S2, S1, not_12_out, ON, not_13_out);
  and and_7 (and_7_out, not_14_out, S2, S1, S0, COMPT5, not_15_out, not_16_out);
  and and_8 (and_8_out, S3, not_21_out, not_22_out, not_23_out, COMPS);
  and and_9 (and_9_out, S3, not_24_out, not_25_out, S0, or_1_out);
  and and_10 (and_10_out, S3, not_26_out, S1, not_27_out, or_2_out);
  and and_11 (and_11_out, S3, S2, S1, S0, not_18_out, not_19_out, not_20_out);
  or or_3 (N3, and_4_out, and_5_out, and_6_out, and_7_out, and_8_out, and_9_out, and_10_out, and_11_out);
endmodule

module Contador_5s (
  input  CLK,
  input  CLR,
  output C0,
  output C1,
  output C2
);

  wire and_1_out, ENABLE_out, pull_resistor_1_node;

  Pull_Resistor #(.pull(1)) pull_resistor_1 (.node(pull_resistor_1_node));
  nand ENABLE (ENABLE_out, C0, C2);
  J_K_Flip_Flop j_k_ff_1 (
    .J(pull_resistor_1_node), .clk(CLK), .K(pull_resistor_1_node), .Q(C0), .en(ENABLE_out), .reset(CLR));  // open: Qn, preset
  J_K_Flip_Flop j_k_ff_2 (.J(C0), .clk(CLK), .K(C0), .Q(C1), .en(ENABLE_out), .reset(CLR));  // open: Qn, preset
  and and_1 (and_1_out, C0, C1);
  J_K_Flip_Flop j_k_ff_3 (
    .J(and_1_out), .clk(CLK), .K(and_1_out), .Q(C2), .en(ENABLE_out), .reset(CLR));  // open: Qn, preset
endmodule

module R (
  input  S3,
  input  S2,
  input  S1,
  input  S0,
  output R
);

  wire and_1_out, and_2_out, not_1_out, not_2_out, not_3_out, not_4_out;

  not not_1 (not_1_out, S3);
  and and_1 (and_1_out, not_1_out, not_2_out);
  not not_2 (not_2_out, S0);
  not not_3 (not_3_out, S2);
  and and_2 (and_2_out, not_3_out, S1, not_4_out);
  not not_4 (not_4_out, S0);
  or or_1 (R, and_1_out, and_2_out);
endmodule

module G (
  input  S3,
  input  S2,
  input  S1,
  input  S0,
  output G
);

  wire not_1_out, not_2_out;

  not not_1 (not_1_out, S2);
  not not_2 (not_2_out, S1);
  and and_1 (G, S3, not_1_out, not_2_out, S0);
  B b_1 ();  // open: S3, S2, S1, S0, B
endmodule

module B (
  input  S3,
  input  S2,
  input  S1,
  input  S0,
  output B
);

  wire and_1_out, and_2_out, and_3_out, not_1_out, not_2_out, not_3_out, not_4_out;

  not not_1 (not_1_out, S3);
  not not_2 (not_2_out, S2);
  not not_3 (not_3_out, S1);
  not not_4 (not_4_out, S0);
  and and_1 (and_1_out, not_1_out, S0);
  or or_1 (B, and_1_out, and_2_out, and_3_out);
  and and_2 (and_2_out, S2, S1, S0);
  and and_3 (and_3_out, S3, not_2_out, not_3_out, not_4_out);
endmodule

module OUT (
  input  S3,
  input  S2,
  input  S1,
  input  S0,
  output OUT
);

  wire not_1_out, not_2_out;

  not not_1 (not_1_out, S2);
  not not_2 (not_2_out, S1);
  and and_1 (OUT, S3, not_1_out, not_2_out, S0);
endmodule

module TELA (
  input  S3,
  input  S2,
  input  S1,
  input  S0,
  output VALOR,
  output P1,
  output P2
);

  wire and_1_out, and_2_out, and_3_out, not_1_out, not_2_out, not_3_out, not_4_out, not_5_out, not_6_out,
       not_7_out;

  not not_1 (not_1_out, S2);
  and and_1 (and_1_out, not_1_out, not_2_out, not_3_out);
  not not_2 (not_2_out, S1);
  not not_3 (not_3_out, S0);
  not not_4 (not_4_out, S3);
  and and_2 (and_2_out, not_4_out, S1);
  not not_5 (not_5_out, S3);
  and and_3 (and_3_out, not_5_out, S2);
  and and_4 (P1, S3, S2, S1, S0);
  not not_6 (not_6_out, S2);
  not not_7 (not_7_out, S1);
  or or_1 (VALOR, and_1_out, and_2_out, and_3_out);
  and and_5 (P2, S3, not_6_out, not_7_out, S0);
endmodule

module Comparado_8_bits (
  input  A0,
  input  B0,
  input  A1,
  input  B1,
  input  A2,
  input  B2,
  input  A3,
  input  B3,
  input  A4,
  input  B4,
  input  A5,
  input  B5,
  input  A6,
  input  B6,
  input  A7,
  input  B7,
  output out_17,
  output A___B,
  output A___B_2
);

  wire a0_b0, a1_b1, a2_b2, a3_b3, a4_b4, a5_b5, a6_b6, a7_b7, and_1_out, and_2_out, and_3_out, and_4_out,
       and_5_out, and_6_out, and_8_out, and_10_out, and_12_out, and_13_out, lsb_a_b, lsb_a_b_t, lsb_a_b_t_t,
       msb_a_b, msb_a_b_t, msb_a_b_t_t;

  xnor xnor_1 (a0_b0, A0, B0);
  xnor xnor_2 (a1_b1, A1, B1);
  xnor xnor_3 (a2_b2, A2, B2);
  xnor xnor_4 (a4_b4, A4, B4);
  xnor xnor_5 (a3_b3, A3, B3);
  xnor xnor_6 (a5_b5, A5, B5);
  xnor xnor_7 (a6_b6, A6, B6);
  xnor xnor_8 (a7_b7, A7, B7);
  and and_1 (and_1_out, a7_b7, A6, ~B6);  // AND_Gate
  and and_2 (and_2_out, A7, ~B7);  // AND_Gate
  and and_3 (and_3_out, a2_b2, a3_b3, A1, ~B1);  // AND_Gate
  and and_4 (and_4_out, a3_b3, A2, ~B2);  // AND_Gate
  and and_5 (and_5_out, A3, ~B3);  // AND_Gate
  and and_6 (and_6_out, a6_b6, a7_b7, A5, ~B5);  // AND_Gate
  and and_7 (lsb_a_b_t, a0_b0, a1_b1, a2_b2, a3_b3);
  and and_8 (and_8_out, A0, ~B0, a1_b1, a2_b2, a3_b3);  // AND_Gate
  and and_9 (msb_a_b_t, a4_b4, a5_b5, a6_b6, a7_b7);
  and and_10 (and_10_out, A4, ~B4, a5_b5, a6_b6, a7_b7);  // AND_Gate
  or or_1 (lsb_a_b_t_t, and_8_out, and_3_out, and_4_out, and_5_out);
  or or_2 (msb_a_b_t_t, and_10_out, and_6_out, and_1_out, and_2_out);
  nor nor_1 (msb_a_b, msb_a_b_t, msb_a_b_t_t);
  nor nor_2 (lsb_a_b, lsb_a_b_t, lsb_a_b_t_t);
  and and_11 (out_17, lsb_a_b_t, msb_a_b_t);
  and and_12 (and_12_out, lsb_a_b, msb_a_b_t);
  and and_13 (and_13_out, lsb_a_b_t_t, msb_a_b_t);
  or or_3 (A___B, and_12_out, msb_a_b);
  or or_4 (A___B_2, and_13_out, msb_a_b_t_t);

  // Notes on the sheet:
  //   A = B
  //   A = B
  //   A > B
  //   A > B
  //   A < B
  //   A < B
  //   MSB
  //   LSB
  //   A = B
  //   SAÍDAS FINAIS
endmodule
