// Logisim project Contador_Inteligente.circ as structural Verilog: 9 circuits, main circuit main
module main (
  input  in_1,
  input  in_2,
  input  in_3,
  input  in_4,
  input  in_5,
  input  in_6,
  input  in_7,
  input  in_8,
  input  in_9,
  input  in_10,
  input  in_11,
  input  in_12,
  input  in_13,
  input  in_14,
  input  in_15,
  input  in_16,
  output [3:0] LSB,
  output [3:0] MSB,
  output [3:0] DEZENAS,
  output [3:0] CENTENAS,
  output [3:0] out_21,
  output [3:0] DEZENAS_2
);

  wire A, a_t, AC, and_1_out, and_2_out, B, b_t, BC, C, c_t, CC, CLK, D, d_t, DC, E, e_t, EC, F, f_t, FC, G,
       g_t, GC, multiplexer_1_out, or_1_out, or_2_out, pull_resistor_1_node, pull_resistor_2_node,
       RESET_CONT_MAX, RESET_CONT_MIN;
  wire [3:0] PASSO, Q0, Q1, Q2;

  Clock clock_1 (.out(CLK));
  and and_1 (and_1_out, in_13, ~in_15);  // AND_Gate
  MX_MI mx_mi_1 (
    .UNIDADES(DEZENAS_2), .UNIDADES_2(LSB), .DEZENAS_3(CENTENAS), .DEZENAS_4(DEZENAS), .in_1(CLK),
    .out_14(MSB), .out_15(out_21), .DEZENAS({in_12, in_11, in_10, in_9}),
    .DEZENAS_2({in_12, in_11, in_10, in_9}), .in_6({in_8, in_7, in_6, in_5}),
    .in_7({in_8, in_7, in_6, in_5}), .in_2(in_14), .in_3(and_1_out), .in_8({in_4, in_3, in_2, in_1}),
    .in_9({in_4, in_3, in_2, in_1}));
  and and_2 (and_2_out, in_13, in_15);
  Armazenador_de_bits armazenador_de_bits_1 (
    .in_2(CLK), .in_7(in_4), .A0(PASSO[0]), .A1(PASSO[1]), .A2(PASSO[2]), .A3(PASSO[3]), .in_3(and_2_out),
    .in_6(in_3), .in_5(in_2), .in_1(in_1));  // open: in_4
  Pull_Resistor pull_resistor_1 (.node(pull_resistor_1_node));
  Multiplexer #(.enable("false")) multiplexer_1 (
    .in0(pull_resistor_1_node), .in1(CLK), .out(multiplexer_1_out), .sel(in_16));
  or or_1 (or_1_out, RESET_CONT_MAX, in_13);
  Contador_crescente contador_crescente_1 (
    .in_4(PASSO), .out_7(Q0), .in_1(or_1_out), .out_8(Q1), .out_9(Q2), .in_2(DEZENAS_2), .in_5(CENTENAS),
    .in_6(MSB), .in_3(multiplexer_1_out));
  Pull_Resistor #(.pull(1)) pull_resistor_2 (.node(pull_resistor_2_node));
  // _7448 7448_1: pin names not known; wires that end beside it: Q0[1], Q0[2], pull_resistor_2_node, pull_resistor_2_node, pull_resistor_2_node, Q0[3], Q0[0], f_t, g_t, a_t, b_t, c_t, d_t, e_t
  LED led_1 (
    .in_1(Q2), .in_4(MSB), .in_2(Q1), .in_5(CENTENAS), .in_3(Q0), .in_6(DEZENAS_2), .out_8(RESET_CONT_MIN));  // open: out_7
  LED led_2 (
    .in_1(Q2), .in_4(out_21), .in_2(Q1), .in_5(DEZENAS), .in_3(Q0), .in_6(LSB), .out_7(RESET_CONT_MAX));  // open: out_8
  // _7448 7448_2: pin names not known; wires that end beside it: Q1[1], Q1[2], pull_resistor_2_node, pull_resistor_2_node, pull_resistor_2_node, Q1[3], Q1[0], F, G, A, B, C, D, E
  or or_2 (or_2_out, RESET_CONT_MIN, RESET_CONT_MAX);
  // _7448 7448_3: pin names not known; wires that end beside it: Q2[1], Q2[2], pull_resistor_2_node, pull_resistor_2_node, pull_resistor_2_node, Q2[3], Q2[0], FC, GC, AC, BC, CC, DC, EC
  LED_part led_3 (.in(or_2_out));
  _7_Segment_Display u_7_segment_display_1 (.g(G), .f(F), .a(A), .b(B), .e(E), .d(D), .c(C));  // open: dp
  _7_Segment_Display u_7_segment_display_2 (.g(GC), .f(FC), .a(AC), .b(BC), .e(EC), .d(DC), .c(CC));  // open: dp
  _7_Segment_Display u_7_segment_display_3 (.g(g_t), .f(f_t), .a(a_t), .b(b_t), .e(e_t), .d(d_t), .c(c_t));  // open: dp

  // Other names for the same wires on the sheet: A0C = in_9; A1C = in_10; A2C = in_11; A3C = in_12; A0D = in_5;
  //   A1D = in_6; A2D = in_7; A3D = in_8; A0U = in_1; A1U = in_2; A2U = in_3; A3U = in_4; DFF[3:0] = CENTENAS;
  //   DFFMX[3:0] = DEZENAS; UFF[3:0] = DEZENAS_2; LOAD = in_13; UFFMX[3:0] = LSB; CFF[3:0] = MSB; MX_MI = in_14;
  //   CFFMX[3:0] = out_21; STEP = in_15; UP_DOWN = in_16

  // Notes on the sheet:
  //   UNIDADES
  //   DEZENAS
  //   CENTENAS
  //   CENTENAS
  //   MSB
  //   UNIDADES
  //   LSB
  //   UNIDADES
endmodule

module Armazenador_de_bits_Com_LOAD (
  input  in_1,
  input  in_2,
  input  in_3,
  input  in_4,
  input  in_5,
  input  in_6,
  input  in_7,
  input  in_8,
  input  in_9,
  input  in_10,
  input  in_11,
  input  in_12,
  input  in_13,
  input  in_14,
  output LSB,
  output LSB_2,
  output LSB_3,
  output out_18,
  output out_19,
  output out_20,
  output out_21,
  output out_22,
  output out_23,
  output out_24,
  output MSB,
  output MSB_2
);

  wire multiplexer_1_out, multiplexer_2_out, multiplexer_3_out, multiplexer_4_out, multiplexer_5_out,
       multiplexer_6_out, multiplexer_7_out, multiplexer_8_out, multiplexer_9_out, multiplexer_10_out,
       multiplexer_11_out, multiplexer_12_out;

  D_Flip_Flop d_ff_1 (.clk(in_13), .D(multiplexer_1_out), .Q(LSB));  // open: Qn, preset, en, reset
  Multiplexer #(.enable("false")) multiplexer_1 (.in0(LSB), .in1(in_1), .out(multiplexer_1_out), .sel(in_14));
  D_Flip_Flop d_ff_2 (.clk(in_13), .D(multiplexer_2_out), .Q(out_18));  // open: Qn, preset, en, reset
  Multiplexer #(.enable("false")) multiplexer_2 (.in0(out_18), .in1(in_4), .out(multiplexer_2_out), .sel(in_14));
  D_Flip_Flop d_ff_3 (.clk(in_13), .D(multiplexer_3_out), .Q(out_21));  // open: Qn, preset, en, reset
  Multiplexer #(.enable("false")) multiplexer_3 (.in0(out_21), .in1(in_7), .out(multiplexer_3_out), .sel(in_14));
  D_Flip_Flop d_ff_4 (.clk(in_13), .D(multiplexer_4_out), .Q(out_24));  // open: Qn, preset, en, reset
  Multiplexer #(.enable("false")) multiplexer_4 (.in0(out_24), .in1(in_10), .out(multiplexer_4_out), .sel(in_14));
  D_Flip_Flop d_ff_5 (.clk(in_13), .D(multiplexer_5_out), .Q(LSB_2));  // open: Qn, preset, en, reset
  Multiplexer #(.enable("false")) multiplexer_5 (.in0(LSB_2), .in1(in_2), .out(multiplexer_5_out), .sel(in_14));
  D_Flip_Flop d_ff_6 (.clk(in_13), .D(multiplexer_6_out), .Q(out_19));  // open: Qn, preset, en, reset
  Multiplexer #(.enable("false")) multiplexer_6 (.in0(out_19), .in1(in_5), .out(multiplexer_6_out), .sel(in_14));
  D_Flip_Flop d_ff_7 (.clk(in_13), .D(multiplexer_7_out), .Q(out_22));  // open: Qn, preset, en, reset
  Multiplexer #(.enable("false")) multiplexer_7 (.in0(out_22), .in1(in_8), .out(multiplexer_7_out), .sel(in_14));
  D_Flip_Flop d_ff_8 (.clk(in_13), .D(multiplexer_8_out), .Q(MSB));  // open: Qn, preset, en, reset
  Multiplexer #(.enable("false")) multiplexer_8 (.in0(MSB), .in1(in_11), .out(multiplexer_8_out), .sel(in_14));
  Multiplexer #(.enable("false")) multiplexer_9 (.in0(out_23), .in1(in_9), .out(multiplexer_9_out), .sel(in_14));
  Multiplexer #(.enable("false")) multiplexer_10 (.in0(MSB_2), .in1(in_12), .out(multiplexer_10_out), .sel(in_14));
  D_Flip_Flop d_ff_9 (.clk(in_13), .D(multiplexer_11_out), .Q(LSB_3));  // open: Qn, preset, en, reset
  Multiplexer #(.enable("false")) multiplexer_11 (.in0(LSB_3), .in1(in_3), .out(multiplexer_11_out), .sel(in_14));
  D_Flip_Flop d_ff_10 (.clk(in_13), .D(multiplexer_12_out), .Q(out_20));  // open: Qn, preset, en, reset
  Multiplexer #(.enable("false")) multiplexer_12 (.in0(out_20), .in1(in_6), .out(multiplexer_12_out), .sel(in_14));
  D_Flip_Flop d_ff_11 (.clk(in_13), .D(multiplexer_9_out), .Q(out_23));  // open: Qn, preset, en, reset
  D_Flip_Flop d_ff_12 (.clk(in_13), .D(multiplexer_10_out), .Q(MSB_2));  // open: Qn, preset, en, reset

  // Other names for the same wires on the sheet: CLK = in_13; LOAD = in_14

  // Notes on the sheet:
  //   A0
  //   ENTRADA DE CLK
  //   MSB
  //   ENTRADA DE LOAD
  //   A1
  //   A2
endmodule

module MX_MI (
  input  in_1,
  input  in_2,
  input  in_3,
  input  [3:0] DEZENAS,
  input  [3:0] DEZENAS_2,
  input  [3:0] in_6,
  input  [3:0] in_7,
  input  [3:0] in_8,
  input  [3:0] in_9,
  output [3:0] UNIDADES,
  output [3:0] UNIDADES_2,
  output [3:0] DEZENAS_3,
  output [3:0] DEZENAS_4,
  output [3:0] out_14,
  output [3:0] out_15
);

  wire multiplexer_1_out, multiplexer_2_out, not_1_out, pull_resistor_1_node, pull_resistor_2_node;

  Pull_Resistor pull_resistor_1 (.node(pull_resistor_1_node));
  Multiplexer #(.enable("false")) multiplexer_1 (
    .in0(pull_resistor_1_node), .in1(in_1), .out(multiplexer_1_out), .sel(in_2));
  Armazenador_de_bits_Com_LOAD armazenador_de_bits_com_load_1 (
    .in_13(multiplexer_1_out), .in_14(in_3), .in_3(DEZENAS_2[0]), .LSB_3(out_15[0]), .out_20(out_15[1]),
    .in_6(DEZENAS_2[1]), .out_23(out_15[2]), .in_9(DEZENAS_2[2]), .MSB_2(out_15[3]), .in_12(DEZENAS_2[3]),
    .LSB(UNIDADES_2[0]), .in_1(in_9[0]), .out_18(UNIDADES_2[1]), .in_4(in_9[1]), .out_21(UNIDADES_2[2]),
    .out_24(UNIDADES_2[3]), .in_10(in_9[3]), .LSB_2(DEZENAS_4[0]), .in_2(in_7[0]), .out_19(DEZENAS_4[1]),
    .in_5(in_7[1]), .out_22(DEZENAS_4[2]), .in_8(in_7[2]), .MSB(DEZENAS_4[3]), .in_11(in_7[3]), .in_7(in_9[2]));
  Pull_Resistor pull_resistor_2 (.node(pull_resistor_2_node));
  not not_1 (not_1_out, in_2);
  Multiplexer #(.enable("false")) multiplexer_2 (
    .in0(pull_resistor_2_node), .in1(in_1), .out(multiplexer_2_out), .sel(not_1_out));
  Armazenador_de_bits_Com_LOAD armazenador_de_bits_com_load_2 (
    .in_13(multiplexer_2_out), .in_14(in_3), .in_3(DEZENAS[0]), .LSB_3(out_14[0]), .out_20(out_14[1]),
    .in_6(DEZENAS[1]), .out_23(out_14[2]), .in_9(DEZENAS[2]), .MSB_2(out_14[3]), .in_12(DEZENAS[3]),
    .LSB(UNIDADES[0]), .in_1(in_8[0]), .out_18(UNIDADES[1]), .in_4(in_8[1]), .out_21(UNIDADES[2]),
    .out_24(UNIDADES[3]), .in_10(in_8[3]), .LSB_2(DEZENAS_3[0]), .in_2(in_6[0]), .out_19(DEZENAS_3[1]),
    .in_5(in_6[1]), .out_22(DEZENAS_3[2]), .in_8(in_6[2]), .MSB(DEZENAS_3[3]), .in_11(in_6[3]), .in_7(in_8[2]));

  // Other names for the same wires on the sheet: CLK = in_1; LOAD = in_3; MX_MI = in_2

  // Notes on the sheet:
  //   CENTENAS
  //   CENTENAS
  //   MÁXIMO
  //   UNIDADES
  //   CENTENAS
  //   CENTENAS
  //   MÍNIMO
  //   UNIDADES
  //   ENTRADA DE CLK
  //   ENTRADA MX_MI
  //   ENTRADA DE LOAD
endmodule

module Contador_crescente (
  input  in_1,
  input  [3:0] in_2,
  input  in_3,
  input  [3:0] in_4,
  input  [3:0] in_5,
  input  [3:0] in_6,
  output [3:0] out_7,
  output [3:0] out_8,
  output [3:0] out_9
);

  wire A, a_t, AC, B, b_t, BC, C, c_t, CC, D, d_t, DC, E, e_t, EC, F, f_t, FC, G, g_t, GC,
       pull_resistor_1_node, pull_resistor_2_node, somador_bcd_1_out_4, somador_bcd_2_out_4,
       somador_bcd_3_out_4;
  wire [3:0] DUNI, multiplexer_1_out, multiplexer_2_out, multiplexer_3_out, TE, UNI;

  Armazenador_de_bits armazenador_de_bits_1 (
    .in_2(in_3), .in_7(multiplexer_1_out[3]), .A0(UNI[0]), .A1(UNI[1]), .A2(UNI[2]), .A3(UNI[3]),
    .in_3(in_1), .in_6(multiplexer_1_out[2]), .in_5(multiplexer_1_out[1]), .in_1(multiplexer_1_out[0]),
    .in_4(in_2));
  Multiplexer #(.width(4), .disabled(0), .enable("false")) multiplexer_1 (
    .in0(out_7), .in1(UNI), .out(multiplexer_1_out), .sel(in_1));
  Pull_Resistor pull_resistor_1 (.node(pull_resistor_1_node));
  Armazenador_de_bits armazenador_de_bits_2 (
    .in_2(in_3), .in_7(multiplexer_2_out[3]), .A0(DUNI[0]), .A1(DUNI[1]), .A2(DUNI[2]), .A3(DUNI[3]),
    .in_3(in_1), .in_6(multiplexer_2_out[2]), .in_5(multiplexer_2_out[1]), .in_1(multiplexer_2_out[0]),
    .in_4(in_5));
  Armazenador_de_bits armazenador_de_bits_3 (
    .in_2(in_3), .in_7(multiplexer_3_out[3]), .A0(TE[0]), .A1(TE[1]), .A2(TE[2]), .A3(TE[3]), .in_3(in_1),
    .in_6(multiplexer_3_out[2]), .in_5(multiplexer_3_out[1]), .in_1(multiplexer_3_out[0]), .in_4(in_6));
  Somador_bcd somador_bcd_1 (
    .in_2(UNI), .in_3(in_4), .out_5(out_7), .out_4(somador_bcd_1_out_4), .in_1(pull_resistor_1_node));
  Multiplexer #(.width(4), .disabled(0), .enable("false")) multiplexer_2 (
    .in0(DUNI), .in1(out_8), .out(multiplexer_2_out), .sel(somador_bcd_1_out_4));
  Multiplexer #(.width(4), .disabled(0), .enable("false")) multiplexer_3 (
    .in0(TE), .in1(out_9), .out(multiplexer_3_out), .sel(somador_bcd_2_out_4));
  Somador_bcd somador_bcd_2 (
    .in_2(DUNI), .in_3(4'b0000), .out_5(out_8), .out_4(somador_bcd_2_out_4), .in_1(somador_bcd_1_out_4));
  Somador_bcd somador_bcd_3 (
    .in_2(TE), .in_3(4'b0000), .out_5(out_9), .out_4(somador_bcd_3_out_4), .in_1(somador_bcd_2_out_4));
  _7_Segment_Display u_7_segment_display_1 (.g(GC), .f(FC), .a(AC), .b(BC), .e(EC), .d(DC), .c(CC));  // open: dp
  _7_Segment_Display u_7_segment_display_2 (.g(G), .f(F), .a(A), .b(B), .e(E), .d(D), .c(C));  // open: dp
  _7_Segment_Display u_7_segment_display_3 (.g(g_t), .f(f_t), .a(a_t), .b(b_t), .e(e_t), .d(d_t), .c(c_t));  // open: dp
  Pull_Resistor #(.pull(1)) pull_resistor_2 (.node(pull_resistor_2_node));
  // _7448 7448_1: pin names not known; wires that end beside it: UNI[1], UNI[2], pull_resistor_2_node, pull_resistor_2_node, pull_resistor_2_node, UNI[3], UNI[0], f_t, g_t, a_t, b_t, c_t, d_t, e_t
  // _7448 7448_2: pin names not known; wires that end beside it: DUNI[1], DUNI[2], pull_resistor_2_node, pull_resistor_2_node, pull_resistor_2_node, DUNI[3], DUNI[0], F, G, A, B, C, D, E
  // _7448 7448_3: pin names not known; wires that end beside it: TE[1], TE[2], pull_resistor_2_node, pull_resistor_2_node, pull_resistor_2_node, TE[3], TE[0], FC, GC, AC, BC, CC, DC, EC

  // Other names for the same wires on the sheet: CLK = in_3; R = in_1
endmodule

module Armazenador_de_bits (
  input  in_1,
  input  in_2,
  input  in_3,
  input  [3:0] in_4,
  input  in_5,
  input  in_6,
  input  in_7,
  output A0,
  output A1,
  output A2,
  output A3
);

  wire multiplexer_1_out, multiplexer_2_out, multiplexer_3_out, multiplexer_4_out;

  Multiplexer #(.enable("false")) multiplexer_1 (.in0(in_1), .in1(in_4[0]), .out(multiplexer_1_out), .sel(in_3));
  Multiplexer #(.enable("false")) multiplexer_2 (.in0(in_5), .in1(in_4[1]), .out(multiplexer_2_out), .sel(in_3));
  Multiplexer #(.enable("false")) multiplexer_3 (.in0(in_6), .in1(in_4[2]), .out(multiplexer_3_out), .sel(in_3));
  Multiplexer #(.enable("false")) multiplexer_4 (.in0(in_7), .in1(in_4[3]), .out(multiplexer_4_out), .sel(in_3));
  D_Flip_Flop d_ff_1 (.clk(in_2), .D(multiplexer_1_out), .Q(A0));  // open: Qn, preset, en, reset
  D_Flip_Flop d_ff_2 (.clk(in_2), .D(multiplexer_2_out), .Q(A1));  // open: Qn, preset, en, reset
  D_Flip_Flop d_ff_3 (.clk(in_2), .D(multiplexer_3_out), .Q(A2));  // open: Qn, preset, en, reset
  D_Flip_Flop d_ff_4 (.clk(in_2), .D(multiplexer_4_out), .Q(A3));  // open: Qn, preset, en, reset

  // Other names for the same wires on the sheet: CLK = in_2; T = in_4[0]; T1 = in_4[1]; T2 = in_4[2]; T3 = in_4[3];
  //   RESET = in_3

  // Notes on the sheet:
  //   ENTRADA DE CLK
  //   LSB
  //   MSB
endmodule

module Somador_bcd (
  input  in_1,
  input  [3:0] in_2,
  input  [3:0] in_3,
  output out_4,
  output [3:0] out_5
);

  wire c, comparador_de_mag_1_out_11, or_2_out, S0, S1, S2, S3, somador_4bits_1_lsb_3, somador_4bits_1_msb_3,
       somador_4bits_1_out_11, somador_4bits_1_out_12, somador_completo_1_co, somador_completo_2_co,
       somador_completo_3_co, somador_completo_4_co;

  Somador_completo somador_completo_1 (.A(in_2[0]), .B(in_3[0]), .cin(in_1), .co(somador_completo_1_co), .s(S0));
  Somador_completo somador_completo_2 (
    .A(in_2[1]), .B(in_3[1]), .cin(somador_completo_1_co), .co(somador_completo_2_co), .s(S1));
  Somador_completo somador_completo_3 (
    .A(in_2[2]), .B(in_3[2]), .cin(somador_completo_2_co), .co(somador_completo_3_co), .s(S2));
  Somador_completo somador_completo_4 (
    .A(in_2[3]), .B(in_3[3]), .cin(somador_completo_3_co), .co(somador_completo_4_co), .s(S3));
  or or_1 (out_4, somador_completo_4_co, c);
  comparador_de_mag comparador_de_mag_1 (
    .A0(S0), .B0(1'b1), .A1(S1), .B1(1'b0), .A2(S2), .B2(1'b0), .A3(S3), .B3(1'b1),
    .out_11(comparador_de_mag_1_out_11));  // open: out_9, out_10
  or or_2 (or_2_out, comparador_de_mag_1_out_11, somador_completo_4_co);
  Multiplexer #(.enable("false")) multiplexer_1 (.in0(S0), .in1(somador_4bits_1_lsb_3), .out(out_5[0]), .sel(or_2_out));
  Multiplexer #(.enable("false")) multiplexer_2 (
    .in0(S1), .in1(somador_4bits_1_out_11), .out(out_5[1]), .sel(or_2_out));
  somador_4bits somador_4bits_1 (
    .out_11(somador_4bits_1_out_11), .out_12(somador_4bits_1_out_12), .MSB_3(somador_4bits_1_msb_3),
    .MSB(1'b0), .in_2(1'b1), .LSB(1'b1), .in_4(1'b0), .MSB_2(S3), .in_6(S2), .LSB_2(S1), .in_8(S0),
    .LSB_3(somador_4bits_1_lsb_3), .in_9(or_2_out), .out_14(c));
  Multiplexer #(.enable("false")) multiplexer_3 (
    .in0(S2), .in1(somador_4bits_1_out_12), .out(out_5[2]), .sel(or_2_out));
  Multiplexer #(.enable("false")) multiplexer_4 (.in0(S3), .in1(somador_4bits_1_msb_3), .out(out_5[3]), .sel(or_2_out));

  // Other names for the same wires on the sheet: A0 = in_2[0]; A1 = in_2[1]; A2 = in_2[2]; A3 = in_2[3]; B0 = in_3[0];
  //   B1 = in_3[1]; B2 = in_3[2]; B3 = in_3[3]

  // Notes on the sheet:
  //   CARRY UNI OUT
  //   LSB
  //   MSB
endmodule

module Subtrator_bcd (
  input  [3:0] in_1,
  input  in_2,
  input  [3:0] in_3,
  output out_4,
  output [3:0] out_5
);

  wire c, comparador_de_mag_1_out_11, multiplexer_1_out, multiplexer_2_out, multiplexer_3_out,
       multiplexer_4_out, or_2_out, somador_4bits_1_lsb_3, somador_4bits_1_msb_3, somador_4bits_1_out_11,
       somador_4bits_1_out_12, subtrator_completo_1_to, subtrator_completo_2_to, subtrator_completo_3_to,
       subtrator_completo_4_to, undriven;

  Subtrator_completo subtrator_completo_1 (
    .A(in_1[0]), .B(in_3[0]), .Te(in_2), .To(subtrator_completo_1_to), .s(out_5[0]));
  Subtrator_completo subtrator_completo_2 (
    .A(in_1[1]), .B(in_3[1]), .Te(subtrator_completo_1_to), .To(subtrator_completo_2_to), .s(out_5[1]));
  Subtrator_completo subtrator_completo_3 (
    .A(in_1[2]), .B(in_3[2]), .Te(subtrator_completo_2_to), .To(subtrator_completo_3_to), .s(out_5[2]));
  Subtrator_completo subtrator_completo_4 (
    .A(in_1[3]), .B(in_3[3]), .Te(subtrator_completo_3_to), .To(subtrator_completo_4_to), .s(out_5[3]));
  or or_1 (out_4, subtrator_completo_4_to, c);
  comparador_de_mag comparador_de_mag_1 (
    .A0(out_5[0]), .B0(1'b1), .A1(out_5[1]), .B1(1'b0), .A2(out_5[2]), .B2(1'b0), .A3(out_5[3]), .B3(1'b1),
    .out_11(comparador_de_mag_1_out_11));  // open: out_9, out_10
  or or_2 (or_2_out, comparador_de_mag_1_out_11, undriven);
  Multiplexer #(.enable("false")) multiplexer_1 (
    .in0(out_5[0]), .in1(somador_4bits_1_lsb_3), .out(multiplexer_1_out), .sel(or_2_out));
  Multiplexer #(.enable("false")) multiplexer_2 (
    .in0(out_5[1]), .in1(somador_4bits_1_out_11), .out(multiplexer_2_out), .sel(or_2_out));
  somador_4bits somador_4bits_1 (
    .out_11(somador_4bits_1_out_11), .out_12(somador_4bits_1_out_12), .MSB_3(somador_4bits_1_msb_3),
    .MSB(1'b0), .in_2(1'b1), .LSB(1'b1), .in_4(1'b0), .MSB_2(out_5[3]), .in_6(out_5[2]), .LSB_2(out_5[1]),
    .in_8(out_5[0]), .LSB_3(somador_4bits_1_lsb_3), .in_9(or_2_out), .out_14(c));
  Multiplexer #(.enable("false")) multiplexer_3 (
    .in0(out_5[2]), .in1(somador_4bits_1_out_12), .out(multiplexer_3_out), .sel(or_2_out));
  Multiplexer #(.enable("false")) multiplexer_4 (
    .in0(out_5[3]), .in1(somador_4bits_1_msb_3), .out(multiplexer_4_out), .sel(or_2_out));

  // Other names for the same wires on the sheet: A0 = in_1[0]; A1 = in_1[1]; A2 = in_1[2]; A3 = in_1[3]; B0 = in_3[0];
  //   B1 = in_3[1]; B2 = in_3[2]; B3 = in_3[3]; S0 = out_5[0]; S1 = out_5[1]; S2 = out_5[2]; S3 = out_5[3]

  // Notes on the sheet:
  //   LSB
  //   MSB
endmodule

module Contador_Decrescente (
  input  in_1,
  input  [3:0] in_2,
  input  in_3,
  input  [3:0] in_4,
  input  [3:0] in_5,
  input  [3:0] in_6,
  input  [3:0] in_7,
  output [3:0] out_8,
  output [3:0] out_9,
  output [3:0] out_10
);

  wire A, a_t, AC, B, b_t, BC, C, c_t, CC, D, d_t, DC, E, e_t, EC, F, f_t, FC, G, g_t, GC, n7448_1_p3,
       pull_resistor_1_node, subtrator_bcd_1_out_4, subtrator_bcd_2_out_4, subtrator_bcd_3_out_4;
  wire [3:0] DUNI, multiplexer_1_out, multiplexer_2_out, multiplexer_3_out, TE, undriven, undriven_2, UNI;

  Multiplexer #(.width(4), .disabled(0), .enable("false")) multiplexer_1 (
    .in0(out_8), .in1(in_2), .out(multiplexer_1_out), .sel(in_1));
  Armazenador_de_bits armazenador_de_bits_1 (
    .in_2(in_3), .in_7(multiplexer_1_out[3]), .A0(UNI[0]), .A1(UNI[1]), .A2(UNI[2]), .A3(UNI[3]),
    .in_6(multiplexer_1_out[2]), .in_5(multiplexer_1_out[1]), .in_1(multiplexer_1_out[0]));  // open: in_3, in_4
  Pull_Resistor pull_resistor_1 (.node(pull_resistor_1_node));
  Armazenador_de_bits armazenador_de_bits_2 (
    .in_2(in_3), .in_7(multiplexer_2_out[3]), .A0(DUNI[0]), .A1(DUNI[1]), .A2(DUNI[2]), .A3(DUNI[3]),
    .in_6(multiplexer_2_out[2]), .in_5(multiplexer_2_out[1]), .in_1(multiplexer_2_out[0]));  // open: in_3, in_4
  Armazenador_de_bits armazenador_de_bits_3 (
    .in_2(in_3), .in_7(multiplexer_3_out[3]), .A0(TE[0]), .A1(TE[1]), .A2(TE[2]), .A3(TE[3]),
    .in_6(multiplexer_3_out[2]), .in_5(multiplexer_3_out[1]), .in_1(multiplexer_3_out[0]));  // open: in_3, in_4
  Subtrator_bcd subtrator_bcd_1 (
    .in_1(UNI), .in_2(pull_resistor_1_node), .in_3(in_4), .out_4(subtrator_bcd_1_out_4), .out_5(out_8));
  Multiplexer #(.width(4), .disabled(0), .enable("false")) multiplexer_2 (
    .in0(DUNI), .in1(undriven_2), .out(multiplexer_2_out), .sel(subtrator_bcd_1_out_4));
  Multiplexer #(.width(4), .disabled(0), .enable("false")) multiplexer_3 (
    .in0(TE), .in1(in_6), .out(multiplexer_3_out), .sel(subtrator_bcd_2_out_4));
  Subtrator_bcd subtrator_bcd_2 (
    .in_1(DUNI), .in_2(subtrator_bcd_1_out_4), .in_3(in_5), .out_4(subtrator_bcd_2_out_4), .out_5(out_9));
  Subtrator_bcd subtrator_bcd_3 (
    .in_1(undriven), .in_2(subtrator_bcd_2_out_4), .in_3(in_7), .out_4(subtrator_bcd_3_out_4), .out_5(out_10));
  _7_Segment_Display u_7_segment_display_1 (.g(GC), .f(FC), .a(AC), .b(BC), .e(EC), .d(DC), .c(CC));  // open: dp
  _7_Segment_Display u_7_segment_display_2 (.g(G), .f(F), .a(A), .b(B), .e(E), .d(D), .c(C));  // open: dp
  _7_Segment_Display u_7_segment_display_3 (.g(g_t), .f(f_t), .a(a_t), .b(b_t), .e(e_t), .d(d_t), .c(c_t));  // open: dp
  // _7448 7448_1: pin names not known; wires that end beside it: UNI[1], UNI[2], n7448_1_p3, n7448_1_p3, n7448_1_p3, UNI[3], UNI[0], f_t, g_t, a_t, b_t, c_t, d_t, e_t
  Pull_Resistor #(.pull(1)) pull_resistor_2 (.node(n7448_1_p3));
  // _7448 7448_2: pin names not known; wires that end beside it: DUNI[1], DUNI[2], n7448_1_p3, n7448_1_p3, n7448_1_p3, DUNI[3], DUNI[0], F, G, A, B, C, D, E
  // _7448 7448_3: pin names not known; wires that end beside it: TE[1], TE[2], n7448_1_p3, n7448_1_p3, n7448_1_p3, TE[3], TE[0], FC, GC, AC, BC, CC, DC, EC

  // Other names for the same wires on the sheet: CLK = in_3
endmodule

module LED (
  input  [3:0] in_1,
  input  [3:0] in_2,
  input  [3:0] in_3,
  input  [3:0] in_4,
  input  [3:0] in_5,
  input  [3:0] in_6,
  output out_7,
  output out_8
);

  wire AC_BC, AC_BC_t, AC_BC_t_t, AD_BD, AD_BD_t, AD_BD_t_t, and_1_out, and_2_out, and_3_out, and_4_out,
       and_5_out, and_6_out, AU_BU, AU_BU_t, AU_BU_t_t;

  comparador_de_mag comparador_de_mag_1 (
    .A0(in_1[0]), .B0(in_4[0]), .A1(in_1[1]), .B1(in_4[1]), .A2(in_1[2]), .B2(in_4[2]), .A3(in_1[3]),
    .B3(in_4[3]), .out_9(AC_BC_t), .out_11(AC_BC_t_t), .out_10(AC_BC));
  and and_1 (and_1_out, AC_BC_t, AD_BD_t, AU_BU_t);
  and and_2 (and_2_out, AC_BC_t, AD_BD_t_t);
  and and_3 (and_3_out, AC_BC_t, AD_BD_t, AU_BU_t_t);
  comparador_de_mag comparador_de_mag_2 (
    .A0(in_2[0]), .B0(in_5[0]), .A1(in_2[1]), .B1(in_5[1]), .A2(in_2[2]), .B2(in_5[2]), .A3(in_2[3]),
    .B3(in_5[3]), .out_9(AD_BD_t), .out_11(AD_BD_t_t), .out_10(AD_BD));
  or or_1 (out_7, AC_BC_t_t, and_1_out, and_2_out, and_3_out);
  comparador_de_mag comparador_de_mag_3 (
    .A0(in_3[0]), .B0(in_6[0]), .A1(in_3[1]), .B1(in_6[1]), .A2(in_3[2]), .B2(in_6[2]), .A3(in_3[3]),
    .B3(in_6[3]), .out_9(AU_BU_t), .out_11(AU_BU_t_t), .out_10(AU_BU));
  and and_4 (and_4_out, AC_BC_t, AD_BD_t, AU_BU_t);
  and and_5 (and_5_out, AC_BC_t, AD_BD);
  and and_6 (and_6_out, AC_BC_t, AD_BD_t, AU_BU);
  or or_2 (out_8, AC_BC, and_4_out, and_5_out, and_6_out);
endmodule
