// Logisim project Matriz_de_led_Sequencial.circ as structural Verilog: 11 circuits, main circuit main
module main (
  input  [3:0] in_1
);

  wire clock_1_out;
  wire [3:0] contador_sincrono_1_out_2;
  wire [7:0] demultiplexer_1_out3, demultiplexer_1_out4, demultiplexer_1_out5, demultiplexer_1_out6,
       demultiplexer_1_out7, demultiplexer_1_out8, demultiplexer_1_out9, demultiplexer_1_out10, l8_1_out_3;

  Clock clock_1 (.out(clock_1_out));
  Contador_Sincrono contador_sincrono_1 (
    .CLK(clock_1_out), .out_2(contador_sincrono_1_out_2[0]), .out_3(contador_sincrono_1_out_2[1]),
    .out_4(contador_sincrono_1_out_2[2]), .out_5(contador_sincrono_1_out_2[3]));
  L2 l2_1 (.in_1(in_1), .in_2(contador_sincrono_1_out_2), .out_3(l8_1_out_3[6]));
  L3 l3_1 (.in_1(in_1), .in_2(contador_sincrono_1_out_2), .out_3(l8_1_out_3[5]));
  L4 l4_1 (.in_1(in_1), .in_2(contador_sincrono_1_out_2), .out_3(l8_1_out_3[4]));
  L5 l5_1 (.in_1(in_1), .in_2(contador_sincrono_1_out_2), .out_3(l8_1_out_3[3]));
  L6 l6_1 (.in_1(in_1), .in_2(contador_sincrono_1_out_2), .out_3(l8_1_out_3[2]));
  L7 l7_1 (.in_1(in_1), .in_2(contador_sincrono_1_out_2), .out_3(l8_1_out_3[1]));
  L8 l8_1 (.in_1(in_1), .in_2(contador_sincrono_1_out_2), .out_3(l8_1_out_3[0]));
  // Probe on contador_sincrono_1_out_2
  Pull_Resistor pull_resistor_1 (.node(l8_1_out_3[7]));
  DotMatrix #(.matrixcols(8), .matrixrows(8)) dotmatrix_1 (
    .col0(demultiplexer_1_out3), .col1(demultiplexer_1_out4), .col2(demultiplexer_1_out5),
    .col3(demultiplexer_1_out6), .col4(demultiplexer_1_out7), .col5(demultiplexer_1_out8),
    .col6(demultiplexer_1_out9), .col7(demultiplexer_1_out10));
  Demultiplexer #(.select(4), .width(8), .enable("false")) demultiplexer_1 (
    .out3(demultiplexer_1_out3), .out4(demultiplexer_1_out4), .out5(demultiplexer_1_out5),
    .out6(demultiplexer_1_out6), .out7(demultiplexer_1_out7), .out8(demultiplexer_1_out8),
    .out9(demultiplexer_1_out9), .out10(demultiplexer_1_out10), .in(l8_1_out_3),
    .sel(contador_sincrono_1_out_2));  // open: out0, out1, out2, out11, out12, out13, out14, out15
endmodule

module Entrada (
  input  D,
  input  C,
  input  B,
  input  A,
  output out_5,
  output out_6,
  output out_7,
  output out_8,
  output out_9,
  output out_10,
  output out_11,
  output out_12,
  output out_13,
  output out_14
);

  and _0 (out_5, ~A, ~B, ~C, ~D);  // AND_Gate
  and _1 (out_6, A, ~B, ~C, ~D);  // AND_Gate
  and _2 (out_7, ~A, B, ~C, ~D);  // AND_Gate
  and _3 (out_8, A, B, ~C, ~D);  // AND_Gate
  and _4 (out_9, ~A, ~B, C, ~D);  // AND_Gate
  and _5 (out_10, A, ~B, C, ~D);  // AND_Gate
  and _6 (out_11, ~A, B, C, ~D);  // AND_Gate
  and _7 (out_12, A, B, C, ~D);  // AND_Gate
  and _8 (out_13, ~A, ~B, ~C, D);  // AND_Gate
  and _9 (out_14, A, ~B, ~C, D);  // AND_Gate

  // Notes on the sheet:
  //   MSB
  //   LSB
endmodule

module Contador_Sincrono (
  input  CLK,
  output out_2,
  output out_3,
  output out_4,
  output out_5
);

  wire and_1_out, and_2_out, pull_resistor_1_node;

  Pull_Resistor #(.pull(1)) pull_resistor_1 (.node(pull_resistor_1_node));
  J_K_Flip_Flop j_k_ff_1 (
    .J(pull_resistor_1_node), .clk(CLK), .K(pull_resistor_1_node), .Q(out_2));  // open: Qn, preset, en, reset
  J_K_Flip_Flop j_k_ff_2 (.J(out_2), .clk(CLK), .K(out_2), .Q(out_3));  // open: Qn, preset, en, reset
  and and_1 (and_1_out, out_2, out_3);
  J_K_Flip_Flop j_k_ff_3 (.J(and_1_out), .clk(CLK), .K(and_1_out), .Q(out_4));  // open: Qn, preset, en, reset
  and and_2 (and_2_out, and_1_out, out_4);
  J_K_Flip_Flop j_k_ff_4 (.J(and_2_out), .clk(CLK), .K(and_2_out), .Q(out_5));  // open: Qn, preset, en, reset
endmodule

module L2 (
  input  [3:0] in_1,
  input  [3:0] in_2,
  output out_3
);

  wire _0, _1, _2, _3, _4, _5, _6, _7, _8, _9, C3, C4, C5, C6, C7, L201, L202, L203, L204, L205, or_1_out,
       or_2_out, or_3_out, or_4_out, or_5_out;

  and and_1 (L202, _1, C5);
  and and_2 (L203, _4, C6);
  Entrada entrada_1 (
    .out_5(_0), .out_6(_1), .out_7(_2), .out_8(_3), .out_9(_4), .out_10(_5), .out_11(_6), .out_12(_7),
    .out_13(_8), .out_14(_9), .D(in_1[3]), .C(in_1[2]), .B(in_1[1]), .A(in_1[0]));
  Decoder decoder_1 (
    .out_5(C3), .out_6(C4), .out_7(C5), .out_8(C6), .out_9(C7), .msb(in_2[3]), .in_2(in_2[2]),
    .in_3(in_2[1]), .lsb(in_2[0]));
  or or_1 (or_1_out, _0, _2, _3, _8, _9);
  or or_2 (or_2_out, C4, C5, C6);
  and and_3 (L201, or_1_out, or_2_out);
  or or_3 (or_3_out, _5, _7);
  or or_4 (or_4_out, C3, C4, C5, C6, C7);
  or or_5 (or_5_out, C5, C6);
  or or_6 (out_3, L201, L202, L203, L204, L205);
  and and_4 (L204, or_3_out, or_4_out);
  and and_5 (L205, _6, or_5_out);
endmodule

module L3 (
  input  [3:0] in_1,
  input  [3:0] in_2,
  output out_3
);

  wire _0, _1, _2, _3, _4, _5, _6, _7, _8, _9, C3, C4, C5, C6, C7, L301, L302, L303, L304, L305, L306,
       or_1_out, or_2_out, or_3_out, or_4_out;

  or or_1 (or_1_out, _0, _2, _3, _8, _9);
  or or_2 (or_2_out, C4, C5);
  Entrada entrada_1 (
    .out_5(_0), .out_6(_1), .out_7(_2), .out_8(_3), .out_9(_4), .out_10(_5), .out_11(_6), .out_12(_7),
    .out_13(_8), .out_14(_9), .D(in_1[3]), .C(in_1[2]), .B(in_1[1]), .A(in_1[0]));
  Decoder decoder_1 (
    .out_5(C3), .out_6(C4), .out_7(C5), .out_8(C6), .out_9(C7), .msb(in_2[3]), .in_2(in_2[2]),
    .in_3(in_2[1]), .lsb(in_2[0]));
  or or_3 (or_3_out, C3, C7);
  and and_1 (L302, _1, or_2_out);
  and and_2 (L301, or_1_out, or_3_out);
  or or_4 (or_4_out, C5, C6);
  and and_3 (L305, _6, C4);
  and and_4 (L306, _7, C7);
  and and_5 (L303, _4, or_4_out);
  and and_6 (L304, _5, C3);
  or or_5 (out_3, L301, L302, L303, L304, L305, L306);
endmodule

module L4 (
  input  [3:0] in_1,
  input  [3:0] in_2,
  output out_3
);

  wire _0, _1, _2, _3, _4, _5, _6, _7, _8, _9, C3, C4, C5, C6, C7, L401, L402, L403, L404, L405, L406, L407,
       or_1_out, or_2_out, or_3_out, or_4_out;

  or or_1 (or_1_out, C3, C6, C7);
  or or_2 (or_2_out, _2, _3);
  Entrada entrada_1 (
    .out_5(_0), .out_6(_1), .out_7(_2), .out_8(_3), .out_9(_4), .out_10(_5), .out_11(_6), .out_12(_7),
    .out_13(_8), .out_14(_9), .D(in_1[3]), .C(in_1[2]), .B(in_1[1]), .A(in_1[0]));
  Decoder decoder_1 (
    .out_5(C3), .out_6(C4), .out_7(C5), .out_8(C6), .out_9(C7), .msb(in_2[3]), .in_2(in_2[2]),
    .in_3(in_2[1]), .lsb(in_2[0]));
  and and_1 (L401, _0, or_1_out);
  and and_2 (L402, _1, C5);
  and and_3 (L403, or_2_out, C7);
  or or_3 (or_3_out, C4, C5);
  and and_4 (L404, _4, or_3_out);
  or or_4 (or_4_out, C3, C4, C5, C6);
  and and_5 (L405, _5, or_4_out);
  or or_5 (out_3, L401, L402, L403, L404, L405, L406, L407);
  and and_6 (L406, _6, C3);
  and and_7 (L407, _7, C6);
endmodule

module L5 (
  input  [3:0] in_1,
  input  [3:0] in_2,
  output out_3
);

  wire _0, _1, _2, _3, _4, _5, _6, _7, _8, _9, C3, C4, C5, C6, C7, L501, L502, L503, L504, L505, L506, L507,
       L508, or_1_out, or_2_out, or_3_out, or_4_out, or_5_out, or_6_out, or_7_out, or_8_out;

  or or_1 (or_1_out, C3, C5, C7);
  or or_2 (or_2_out, _1, _7);
  or or_3 (or_3_out, C4, C5);
  Entrada entrada_1 (
    .out_5(_0), .out_6(_1), .out_7(_2), .out_8(_3), .out_9(_4), .out_10(_5), .out_11(_6), .out_12(_7),
    .out_13(_8), .out_14(_9), .D(in_1[3]), .C(in_1[2]), .B(in_1[1]), .A(in_1[0]));
  Decoder decoder_1 (
    .out_5(C3), .out_6(C4), .out_7(C5), .out_8(C6), .out_9(C7), .msb(in_2[3]), .in_2(in_2[2]),
    .in_3(in_2[1]), .lsb(in_2[0]));
  and and_1 (L501, _0, or_1_out);
  and and_2 (L502, or_2_out, C5);
  or or_4 (or_4_out, C3, C4, C5, C6);
  and and_3 (L503, _2, or_3_out);
  and and_4 (L507, _6, or_4_out);
  or or_5 (or_5_out, _3, _8);
  or or_6 (or_6_out, C4, C5, C6);
  or or_7 (or_7_out, C3, C6);
  or or_8 (or_8_out, C4, C5, C6, C7);
  and and_5 (L504, or_5_out, or_6_out);
  and and_6 (L505, _4, or_7_out);
  and and_7 (L506, _5, C6);
  and and_8 (L508, _9, or_8_out);
  or or_9 (out_3, L501, L502, L503, L504, L505, L506, L507, L508);
endmodule

module L6 (
  input  [3:0] in_1,
  input  [3:0] in_2,
  output out_3
);

  wire _0, _1, _2, _3, _4, _5, _6, _7, _8, _9, C3, C4, C5, C6, C7, L601, L602, L603, L604, L605, L606, L607,
       or_1_out, or_2_out, or_3_out, or_4_out, or_5_out, or_6_out;

  or or_1 (or_1_out, C3, C5, C7);
  or or_2 (or_2_out, C3, C7);
  Entrada entrada_1 (
    .out_5(_0), .out_6(_1), .out_7(_2), .out_8(_3), .out_9(_4), .out_10(_5), .out_11(_6), .out_12(_7),
    .out_13(_8), .out_14(_9), .D(in_1[3]), .C(in_1[2]), .B(in_1[1]), .A(in_1[0]));
  Decoder decoder_1 (
    .out_5(C3), .out_6(C4), .out_7(C5), .out_8(C6), .out_9(C7), .msb(in_2[3]), .in_2(in_2[2]),
    .in_3(in_2[1]), .lsb(in_2[0]));
  and and_1 (L601, _0, or_1_out);
  and and_2 (L602, _1, C5);
  or or_3 (or_3_out, _3, _5);
  or or_4 (or_4_out, _6, _8);
  and and_3 (L606, or_4_out, or_2_out);
  and and_4 (L604, or_3_out, C7);
  or or_5 (or_5_out, _2, _7);
  and and_5 (L603, or_5_out, C4);
  or or_6 (or_6_out, C3, C4, C5, C6, C7);
  and and_6 (L607, _9, C7);
  or or_7 (out_3, L601, L602, L603, L604, L605, L606, L607);
  and and_7 (L605, _4, or_6_out);
endmodule

module L7 (
  input  [3:0] in_1,
  input  [3:0] in_2,
  output out_3
);

  wire _0, _1, _2, _3, _4, _5, _6, _7, _8, _9, C3, C4, C5, C6, C7, L701, L702, L703, L704, L705, or_1_out,
       or_2_out, or_3_out;

  or or_1 (or_1_out, _0, _3, _5, _6, _8);
  or or_2 (or_2_out, C3, C7);
  and and_1 (L703, _2, C3);
  Entrada entrada_1 (
    .out_5(_0), .out_6(_1), .out_7(_2), .out_8(_3), .out_9(_4), .out_10(_5), .out_11(_6), .out_12(_7),
    .out_13(_8), .out_14(_9), .D(in_1[3]), .C(in_1[2]), .B(in_1[1]), .A(in_1[0]));
  Decoder decoder_1 (
    .out_5(C3), .out_6(C4), .out_7(C5), .out_8(C6), .out_9(C7), .msb(in_2[3]), .in_2(in_2[2]),
    .in_3(in_2[1]), .lsb(in_2[0]));
  L8 l8_1 ();  // open: in_1, in_2, out_3
  and and_2 (L701, or_1_out, or_2_out);
  and and_3 (L702, _1, C5);
  or or_3 (or_3_out, _4, _9);
  and and_4 (L705, _7, C4);
  or or_4 (out_3, L701, L702, L703, L704, L705);
  and and_5 (L704, or_3_out, C6);
endmodule

module L8 (
  input  [3:0] in_1,
  input  [3:0] in_2,
  output out_3
);

  wire _0, _1, _2, _3, _4, _5, _6, _7, _8, _9, C3, C4, C5, C6, C7, L801, L802, L803, L804, L805, or_1_out,
       or_2_out, or_3_out, or_4_out;

  Entrada entrada_1 (
    .out_5(_0), .out_6(_1), .out_7(_2), .out_8(_3), .out_9(_4), .out_10(_5), .out_11(_6), .out_12(_7),
    .out_13(_8), .out_14(_9), .D(in_1[3]), .C(in_1[2]), .B(in_1[1]), .A(in_1[0]));
  Decoder decoder_1 (
    .out_5(C3), .out_6(C4), .out_7(C5), .out_8(C6), .out_9(C7), .msb(in_2[3]), .in_2(in_2[2]),
    .in_3(in_2[1]), .lsb(in_2[0]));
  or or_1 (or_1_out, _0, _1, _3, _5, _6);
  or or_2 (or_2_out, C4, C5, C6);
  or or_3 (or_3_out, C3, C4, C5, C6, C7);
  and and_1 (L803, _4, C6);
  and and_2 (L801, or_1_out, or_2_out);
  and and_3 (L802, _2, or_3_out);
  or or_4 (or_4_out, C4, C5);
  or or_5 (out_3, L801, L802, L803, L804, L805);
  and and_4 (L804, _7, C4);
  and and_5 (L805, _7, or_4_out);
endmodule

module Decoder (
  input  msb,
  input  in_2,
  input  in_3,
  input  lsb,
  output out_5,
  output out_6,
  output out_7,
  output out_8,
  output out_9
);

  and _3 (out_5, lsb, in_3, ~in_2, ~msb);  // AND_Gate
  and _4 (out_6, ~lsb, ~in_3, in_2, ~msb);  // AND_Gate
  and _5 (out_7, lsb, ~in_3, in_2, ~msb);  // AND_Gate
  and _6 (out_8, ~lsb, in_3, in_2, ~msb);  // AND_Gate
  and _7 (out_9, lsb, in_3, in_2, ~msb);  // AND_Gate
endmodule
