// Logisim project MDE.circ as structural Verilog: 6 circuits, main circuit main
module main (
  input  U,
  input  Y,
  input  in_3,
  output Z
);

  wire A, B, C, clock_1_out, D, E, F, G, log_1_n0, log_1_n1, log_1_n2, pull_resistor_1_node,
       pull_resistor_2_node, registrador_de_estado_1_s0, registrador_de_estado_1_s1,
       registrador_de_estado_1_s2;

  Clock clock_1 (.out(clock_1_out));
  LOG log_1 (
    .U(U), .Y(Y), .S2(registrador_de_estado_1_s2), .S1(registrador_de_estado_1_s1),
    .S0(registrador_de_estado_1_s0), .Z(Z), .N2(log_1_n2), .N1(log_1_n1), .N0(log_1_n0));
  Registrador_de_Estado registrador_de_estado_1 (
    .CLK(clock_1_out), .CLEAR(in_3), .S2(registrador_de_estado_1_s2), .S1(registrador_de_estado_1_s1),
    .S0(registrador_de_estado_1_s0), .N2(log_1_n2), .N1(log_1_n1), .N0(log_1_n0));
  Pull_Resistor #(.pull(1)) pull_resistor_1 (.node(pull_resistor_1_node));
  Pull_Resistor pull_resistor_2 (.node(pull_resistor_2_node));
  // _7448 7448_1: pin names not known; wires that end beside it: registrador_de_estado_1_s1, registrador_de_estado_1_s2, pull_resistor_1_node, pull_resistor_1_node, pull_resistor_1_node, pull_resistor_2_node, registrador_de_estado_1_s0, F, G, A, B, C, D, E
  _7_Segment_Display u_7_segment_display_1 (.g(G), .f(F), .a(A), .b(B), .e(E), .d(D), .c(C));  // open: dp

  // Notes on the sheet:
  //   CLK
  //   CLR
endmodule

module Registrador_de_Estado (
  input  CLK,
  input  N2,
  input  N1,
  input  N0,
  input  CLEAR,
  output S2,
  output S1,
  output S0
);

  D_Flip_Flop d_ff_1 (.clk(CLK), .D(N2), .Q(S2), .reset(CLEAR));  // open: Qn, preset, en
  D_Flip_Flop d_ff_2 (.clk(CLK), .D(N1), .Q(S1), .reset(CLEAR));  // open: Qn, preset, en
  D_Flip_Flop d_ff_3 (.clk(CLK), .D(N0), .Q(S0), .reset(CLEAR));  // open: Qn, preset, en
endmodule

module LOG (
  input  U,
  input  Y,
  input  S2,
  input  S1,
  input  S0,
  output Z,
  output N2,
  output N1,
  output N0
);

  wire and_1_out, and_2_out, and_3_out, and_4_out, and_5_out, and_6_out, and_7_out, and_8_out, and_9_out,
       and_10_out, and_11_out, and_12_out, and_13_out, and_17_out, and_18_out, and_19_out, and_20_out,
       and_21_out, and_22_out, and_23_out, and_24_out, and_25_out, and_26_out, and_27_out, and_28_out,
       and_29_out, and_30_out, and_31_out, and_32_out, and_33_out, and_34_out, and_35_out, and_36_out,
       and_37_out, and_38_out, and_39_out, B, C, D, or_1_out, or_2_out, or_3_out;

  and and_1 (and_1_out, U, ~Y);  // AND_Gate
  and and_2 (and_2_out, ~U, ~Y);  // AND_Gate
  and and_3 (and_3_out, ~S2, ~S1, ~S0, U);  // AND_Gate
  and and_4 (and_4_out, ~S2, ~S1, S0);  // AND_Gate
  and and_5 (and_5_out, U, Y);
  and and_6 (and_6_out, ~U, ~Y);  // AND_Gate
  and and_7 (and_7_out, ~S2, S1, ~S0);  // AND_Gate
  and and_8 (and_8_out, U, Y);
  and and_9 (and_9_out, ~U, Y);  // AND_Gate
  and and_10 (and_10_out, ~S2, S1, S0);  // AND_Gate
  and and_11 (and_11_out, ~U, ~Y);  // AND_Gate
  and and_12 (and_12_out, S2, ~S1, ~S0);  // AND_Gate
  and and_13 (and_13_out, S2, ~S1, S0, ~Y);  // AND_Gate
  and and_14 (B, ~S2, ~S1, S0);  // AND_Gate
  and and_15 (C, ~S2, S1, ~S0);  // AND_Gate
  and and_16 (D, ~S2, S1, S0);  // AND_Gate
  or or_1 (or_1_out, and_5_out, and_6_out);
  or or_2 (or_2_out, and_8_out, and_9_out, ~Y);  // OR_Gate
  or or_3 (or_3_out, and_1_out, and_2_out, Y);
  or or_4 (Z, B, C, D);
  and and_17 (and_17_out, and_4_out, or_1_out);
  and and_18 (and_18_out, and_7_out, or_2_out);
  and and_19 (and_19_out, and_10_out, and_11_out);
  and and_20 (and_20_out, and_12_out, or_3_out);
  or or_5 (N0, and_3_out, and_17_out, and_18_out, and_19_out, and_20_out, and_13_out);
  and and_21 (and_21_out, ~S2, S1, S0);  // AND_Gate
  and and_22 (and_22_out, ~U, ~Y);  // AND_Gate
  and and_23 (and_23_out, S2, ~S1);  // AND_Gate
  and and_24 (and_24_out, U, ~Y);  // AND_Gate
  and and_25 (and_25_out, ~S2, ~S1, ~S0);  // AND_Gate
  and and_26 (and_26_out, U, ~Y);  // AND_Gate
  and and_27 (and_27_out, ~S2, ~S1, S0);  // AND_Gate
  and and_28 (and_28_out, ~U, ~Y);  // AND_Gate
  and and_29 (and_29_out, ~S2, S1, ~S0, ~Y);  // AND_Gate
  and and_30 (and_30_out, ~S2, ~S1, S0, U);  // AND_Gate
  and and_31 (and_31_out, ~S2, S1, ~S0);  // AND_Gate
  and and_32 (and_32_out, U, Y);
  and and_33 (and_33_out, ~S2, S1, S0, U);  // AND_Gate
  and and_34 (and_34_out, S2, ~S1, Y);  // AND_Gate
  and and_35 (and_35_out, and_25_out, and_26_out);
  and and_36 (and_36_out, and_27_out, and_28_out);
  and and_37 (and_37_out, and_21_out, and_22_out);
  and and_38 (and_38_out, and_23_out, and_24_out);
  and and_39 (and_39_out, and_31_out, and_32_out);
  or or_6 (N1, and_35_out, and_36_out, and_29_out, and_37_out, and_38_out);
  or or_7 (N2, and_30_out, and_39_out, and_33_out, and_34_out);
endmodule

module N0 (
  input  U,
  input  Y,
  input  S2,
  input  S1,
  input  S0,
  output Z,
  output N2,
  output N1,
  output N0
);

  wire and_1_out, and_2_out, and_3_out, and_4_out, and_5_out, and_6_out, and_7_out, and_8_out, and_9_out,
       and_10_out, and_11_out, and_12_out, and_13_out, and_14_out, and_15_out, and_16_out, and_17_out,
       or_1_out, or_2_out, or_3_out;

  and and_1 (and_1_out, ~S2, ~S1, ~S0, U);  // AND_Gate
  and and_2 (and_2_out, ~S2, ~S1, S0);  // AND_Gate
  and and_3 (and_3_out, U, Y);
  and and_4 (and_4_out, ~U, ~Y);  // AND_Gate
  and and_5 (and_5_out, ~S2, S1, ~S0);  // AND_Gate
  and and_6 (and_6_out, U, Y);
  and and_7 (and_7_out, ~U, Y);  // AND_Gate
  and and_8 (and_8_out, U, ~Y);  // AND_Gate
  and and_9 (and_9_out, ~U, ~Y);  // AND_Gate
  and and_10 (and_10_out, S2, ~S1, S0, ~Y);  // AND_Gate
  or or_1 (or_1_out, and_3_out, and_4_out);
  or or_2 (or_2_out, and_6_out, and_7_out, ~Y);  // OR_Gate
  and and_11 (and_11_out, ~S2, S1, S0);  // AND_Gate
  and and_12 (and_12_out, ~U, ~Y);  // AND_Gate
  and and_13 (and_13_out, S2, ~S1, ~S0);  // AND_Gate
  or or_3 (or_3_out, and_8_out, and_9_out, Y);
  and and_14 (and_14_out, and_2_out, or_1_out);
  and and_15 (and_15_out, and_5_out, or_2_out);
  and and_16 (and_16_out, and_11_out, and_12_out);
  and and_17 (and_17_out, and_13_out, or_3_out);
  or or_4 (N0, and_1_out, and_14_out, and_15_out, and_16_out, and_17_out, and_10_out);
endmodule

module N1 (
  input  U,
  input  Y,
  input  S2,
  input  S1,
  input  S0,
  output Z,
  output N2,
  output N1,
  output N0
);

  wire and_1_out, and_2_out, and_3_out, and_4_out, and_5_out, and_6_out, and_7_out, and_8_out, and_9_out,
       and_10_out, and_11_out, and_12_out, and_13_out;

  and and_1 (and_1_out, ~S2, S1, S0);  // AND_Gate
  and and_2 (and_2_out, ~U, ~Y);  // AND_Gate
  and and_3 (and_3_out, S2, ~S1);  // AND_Gate
  and and_4 (and_4_out, U, ~Y);  // AND_Gate
  and and_5 (and_5_out, ~S2, ~S1, ~S0);  // AND_Gate
  and and_6 (and_6_out, U, ~Y);  // AND_Gate
  and and_7 (and_7_out, ~S2, ~S1, S0);  // AND_Gate
  and and_8 (and_8_out, ~U, ~Y);  // AND_Gate
  and and_9 (and_9_out, ~S2, S1, ~S0, ~Y);  // AND_Gate
  and and_10 (and_10_out, and_5_out, and_6_out);
  and and_11 (and_11_out, and_7_out, and_8_out);
  and and_12 (and_12_out, and_1_out, and_2_out);
  and and_13 (and_13_out, and_3_out, and_4_out);
  or or_1 (N1, and_10_out, and_11_out, and_9_out, and_12_out, and_13_out);
endmodule

module N2 (
  input  U,
  input  Y,
  input  S2,
  input  S1,
  input  S0,
  output Z,
  output N2,
  output N1,
  output N0
);

  wire and_1_out, and_2_out, and_3_out, and_4_out, and_5_out, and_6_out;

  and and_1 (and_1_out, ~S2, ~S1, S0, U);  // AND_Gate
  and and_2 (and_2_out, ~S2, S1, ~S0);  // AND_Gate
  and and_3 (and_3_out, U, Y);
  and and_4 (and_4_out, ~S2, S1, S0, U);  // AND_Gate
  and and_5 (and_5_out, S2, ~S1, Y);  // AND_Gate
  and and_6 (and_6_out, and_2_out, and_3_out);
  or or_1 (N2, and_1_out, and_6_out, and_4_out, and_5_out);
endmodule
