// Logisim project Maquina_de_vendas.circ as structural Verilog: 7 circuits, main circuit main
module main (
  input  [3:0] A,
  input  [3:0] S,
  output D
);

  wire C_out, CLK, comparator_1_eq, comparator_1_lt, contador_1_clr, logica_c_1_c_out, logica_cont_1_clr,
       logica_cont_1_en;
  wire [3:0] adder_1_out, mem_ld_4b_1_out_11;

  Clock u_CLK (.out(CLK));
  Button C (.out(C_out));
  Logica_c logica_c_1 (.C_in(C_out), .CLK(CLK), .C_out(logica_c_1_c_out));
  Mem_LD_4b mem_ld_4b_1 (
    .CLK(CLK), .LD(logica_c_1_c_out), .CLR(logica_cont_1_clr), .out_8(mem_ld_4b_1_out_11[3]),
    .out_9(mem_ld_4b_1_out_11[2]), .out_10(mem_ld_4b_1_out_11[1]), .out_11(mem_ld_4b_1_out_11[0]),
    .Y3(adder_1_out[3]), .Y2(adder_1_out[2]), .Y1(adder_1_out[1]), .Y0(adder_1_out[0]));
  Contador contador_1 (.EN(logica_cont_1_en), .CLR(contador_1_clr), .CLK(CLK));
  Comparator #(.width(4), .mode("unsigned")) comparator_1 (
    .a(S), .b(mem_ld_4b_1_out_11), .eq(comparator_1_eq), .lt(comparator_1_lt));  // open: gt
  Logica_cont logica_cont_1 (.MD(D), .TC(contador_1_clr), .CLK(CLK), .EN(logica_cont_1_en), .CLR(logica_cont_1_clr));
  Adder #(.width(4)) adder_1 (.a(A), .b(mem_ld_4b_1_out_11), .out(adder_1_out));  // open: cin, cout
  // Probe on adder_1_out
  or or_1 (D, comparator_1_eq, comparator_1_lt);

  // Notes on the sheet:
  //   MDE_botão
  //   Registrador
  //   Contador
  //   Somador
  //   Comparador
  //   MDE_D
endmodule

module Mem_LD (
  input  CLK,
  input  Y,
  input  LD,
  input  CLR,
  output Q
);

  wire multiplexer_1_out;

  Multiplexer #(.enable("false")) multiplexer_1 (.in0(Q), .in1(Y), .out(multiplexer_1_out), .sel(LD));
  D_Flip_Flop FFD (.clk(CLK), .D(multiplexer_1_out), .Q(Q), .reset(CLR));  // open: Qn, preset, en
endmodule

module Mem_LD_4b (
  input  CLK,
  input  Y3,
  input  Y2,
  input  Y1,
  input  Y0,
  input  LD,
  input  CLR,
  output out_8,
  output out_9,
  output out_10,
  output out_11
);

  Mem_LD mem_ld_1 (.CLK(CLK), .Y(Y3), .LD(LD), .Q(out_8), .CLR(CLR));
  Mem_LD mem_ld_2 (.CLK(CLK), .Y(Y2), .LD(LD), .Q(out_9), .CLR(CLR));
  Mem_LD mem_ld_3 (.CLK(CLK), .Y(Y1), .LD(LD), .Q(out_10), .CLR(CLR));
  Mem_LD mem_ld_4 (.CLK(CLK), .Y(Y0), .LD(LD), .Q(out_11), .CLR(CLR));
endmodule

module Contador (
  input  CLK,
  input  EN,
  output CLR
);

  wire and_1_out, and_3_out, and_4_out, and_5_out, C0_q, C1_q, C2_q, C3_q, C4_q, C5_q, pull_resistor_1_node;

  Pull_Resistor #(.pull(1)) pull_resistor_1 (.node(pull_resistor_1_node));
  J_K_Flip_Flop C0 (
    .J(pull_resistor_1_node), .clk(CLK), .K(pull_resistor_1_node), .Q(C0_q), .en(EN), .reset(CLR));  // open: Qn, preset
  J_K_Flip_Flop C1 (.J(C0_q), .clk(CLK), .K(C0_q), .Q(C1_q), .en(EN), .reset(CLR));  // open: Qn, preset
  and and_1 (and_1_out, C0_q, C1_q);
  and and_2 (CLR, C3_q, C5_q);
  J_K_Flip_Flop C2 (.J(and_1_out), .clk(CLK), .K(and_1_out), .Q(C2_q), .en(EN), .reset(CLR));  // open: Qn, preset
  and and_3 (and_3_out, and_1_out, C2_q);
  and and_4 (and_4_out, and_3_out, C3_q);
  J_K_Flip_Flop C3 (.J(and_3_out), .clk(CLK), .K(and_3_out), .Q(C3_q), .en(EN), .reset(CLR));  // open: Qn, preset
  J_K_Flip_Flop C4 (.J(and_4_out), .clk(CLK), .K(and_4_out), .Q(C4_q), .en(EN), .reset(CLR));  // open: Qn, preset
  and and_5 (and_5_out, and_4_out, C4_q);
  J_K_Flip_Flop C5 (.J(and_5_out), .clk(CLK), .K(and_5_out), .Q(C5_q), .en(EN), .reset(CLR));  // open: Qn, preset
endmodule

module Logica_c (
  input  C_in,
  input  CLK,
  output C_out
);

  wire and_2_out, and_3_out, N0_out, N2_out, res_est_2b_1_s0, res_est_2b_1_s1;

  Res_est_2b res_est_2b_1 (.CLK(CLK), .S0(res_est_2b_1_s0), .S1(res_est_2b_1_s1), .N0(N0_out), .N1(N2_out));
  and and_1 (C_out, res_est_2b_1_s1, ~res_est_2b_1_s0);  // AND_Gate
  and N2 (N2_out, ~C_in, ~res_est_2b_1_s1, res_est_2b_1_s0);  // AND_Gate
  and and_2 (and_2_out, C_in, ~res_est_2b_1_s1, res_est_2b_1_s0);  // AND_Gate
  or N0 (N0_out, and_2_out, and_3_out);
  and and_3 (and_3_out, C_in, ~res_est_2b_1_s1, ~res_est_2b_1_s0);  // AND_Gate
endmodule

module Res_est_2b (
  input  CLK,
  input  N0,
  input  N1,
  output S0,
  output S1
);

  D_Flip_Flop d_ff_1 (.clk(CLK), .D(N0), .Q(S0));  // open: Qn, preset, en, reset
  D_Flip_Flop d_ff_2 (.clk(CLK), .D(N1), .Q(S1));  // open: Qn, preset, en, reset
endmodule

module Logica_cont (
  input  MD,
  input  TC,
  input  CLK,
  output EN,
  output CLR
);

  wire and_3_out, and_4_out, or_1_out, res_est_2b_1_s0, res_est_2b_1_s1;

  Res_est_2b res_est_2b_1 (.CLK(CLK), .S0(res_est_2b_1_s0), .S1(res_est_2b_1_s1), .N0(or_1_out));  // open: N1
  and and_1 (EN, ~res_est_2b_1_s1, res_est_2b_1_s0);  // AND_Gate
  and and_2 (CLR, MD, TC, ~res_est_2b_1_s1, res_est_2b_1_s0);  // AND_Gate
  and and_3 (and_3_out, MD, ~TC, ~res_est_2b_1_s1, res_est_2b_1_s0);  // AND_Gate
  and and_4 (and_4_out, MD, ~TC, ~res_est_2b_1_s1, ~res_est_2b_1_s0);  // AND_Gate
  or or_1 (or_1_out, and_3_out, and_4_out);
endmodule
