// Logisim project Maquina_de_troco.circ as structural Verilog
module Memoria_6bits (
  input  CLK,
  input  CLR,
  input  in_3,
  input  [5:0] in_4,
  output [5:0] out_5
);

  D_Flip_Flop d_ff_1 (.clk(CLK), .D(in_4[5]), .Q(out_5[5]), .en(in_3), .reset(CLR));  // open: Qn, preset
  D_Flip_Flop d_ff_2 (.clk(CLK), .D(in_4[4]), .Q(out_5[4]), .en(in_3), .reset(CLR));  // open: Qn, preset
  D_Flip_Flop d_ff_3 (.clk(CLK), .D(in_4[3]), .Q(out_5[3]), .en(in_3), .reset(CLR));  // open: Qn, preset
  D_Flip_Flop d_ff_4 (.clk(CLK), .D(in_4[2]), .Q(out_5[2]), .en(in_3), .reset(CLR));  // open: Qn, preset
  D_Flip_Flop d_ff_5 (.clk(CLK), .D(in_4[1]), .Q(out_5[1]), .en(in_3), .reset(CLR));  // open: Qn, preset
  D_Flip_Flop d_ff_6 (.clk(CLK), .D(in_4[0]), .Q(out_5[0]), .en(in_3), .reset(CLR));  // open: Qn, preset
endmodule

module Memoria_10bits (
  input  CLK,
  input  CLR,
  input  EN,
  input  [9:0] Input,
  output [9:0] OUTPUT
);

  D_Flip_Flop d_ff_1 (.clk(CLK), .D(Input[9]), .Q(OUTPUT[9]), .en(EN), .reset(CLR));  // open: Qn, preset
  D_Flip_Flop d_ff_2 (.clk(CLK), .D(Input[8]), .Q(OUTPUT[8]), .en(EN), .reset(CLR));  // open: Qn, preset
  D_Flip_Flop d_ff_3 (.clk(CLK), .D(Input[7]), .Q(OUTPUT[7]), .en(EN), .reset(CLR));  // open: Qn, preset
  D_Flip_Flop d_ff_4 (.clk(CLK), .D(Input[6]), .Q(OUTPUT[6]), .en(EN), .reset(CLR));  // open: Qn, preset
  D_Flip_Flop d_ff_5 (.clk(CLK), .D(Input[5]), .Q(OUTPUT[5]), .en(EN), .reset(CLR));  // open: Qn, preset
  D_Flip_Flop d_ff_6 (.clk(CLK), .D(Input[4]), .Q(OUTPUT[4]), .en(EN), .reset(CLR));  // open: Qn, preset
  D_Flip_Flop d_ff_7 (.clk(CLK), .D(Input[3]), .Q(OUTPUT[3]), .en(EN), .reset(CLR));  // open: Qn, preset
  D_Flip_Flop d_ff_8 (.clk(CLK), .D(Input[2]), .Q(OUTPUT[2]), .en(EN), .reset(CLR));  // open: Qn, preset
  D_Flip_Flop d_ff_9 (.clk(CLK), .D(Input[1]), .Q(OUTPUT[1]), .en(EN), .reset(CLR));  // open: Qn, preset
  D_Flip_Flop d_ff_10 (.clk(CLK), .D(Input[0]), .Q(OUTPUT[0]), .en(EN), .reset(CLR));  // open: Qn, preset
endmodule

module Memoria_6bits_load (
  input  Load,
  input  CLOCK,
  input  Clear,
  input  [5:0] Entrada,
  output [5:0] Saida
);

  wire multiplexer_1_out, multiplexer_2_out, multiplexer_3_out, multiplexer_4_out, multiplexer_5_out,
       multiplexer_6_out;

  D_Flip_Flop d_ff_1 (.clk(CLOCK), .D(multiplexer_1_out), .Q(Saida[0]), .reset(Clear));  // open: Qn, preset, en
  Multiplexer #(.enable("false")) multiplexer_1 (.in0(Saida[0]), .in1(Entrada[0]), .out(multiplexer_1_out), .sel(Load));
  D_Flip_Flop d_ff_2 (.clk(CLOCK), .D(multiplexer_2_out), .Q(Saida[1]), .reset(Clear));  // open: Qn, preset, en
  Multiplexer #(.enable("false")) multiplexer_2 (.in0(Saida[1]), .in1(Entrada[1]), .out(multiplexer_2_out), .sel(Load));
  D_Flip_Flop d_ff_3 (.clk(CLOCK), .D(multiplexer_3_out), .Q(Saida[2]), .reset(Clear));  // open: Qn, preset, en
  Multiplexer #(.enable("false")) multiplexer_3 (.in0(Saida[2]), .in1(Entrada[2]), .out(multiplexer_3_out), .sel(Load));
  D_Flip_Flop d_ff_4 (.clk(CLOCK), .D(multiplexer_4_out), .Q(Saida[3]), .reset(Clear));  // open: Qn, preset, en
  Multiplexer #(.enable("false")) multiplexer_4 (.in0(Saida[3]), .in1(Entrada[3]), .out(multiplexer_4_out), .sel(Load));
  D_Flip_Flop d_ff_5 (.clk(CLOCK), .D(multiplexer_5_out), .Q(Saida[4]), .reset(Clear));  // open: Qn, preset, en
  Multiplexer #(.enable("false")) multiplexer_5 (.in0(Saida[4]), .in1(Entrada[4]), .out(multiplexer_5_out), .sel(Load));
  D_Flip_Flop d_ff_6 (.clk(CLOCK), .D(multiplexer_6_out), .Q(Saida[5]), .reset(Clear));  // open: Qn, preset, en
  Multiplexer #(.enable("false")) multiplexer_6 (.in0(Saida[5]), .in1(Entrada[5]), .out(multiplexer_6_out), .sel(Load));

  // Notes on the sheet:
  //   LSB
endmodule

module Memoria_10bits_load (
  input  Load,
  input  CLOCK,
  input  Clear,
  input  [9:0] Entrada,
  output [9:0] \Saída 
);

  wire multiplexer_1_out, multiplexer_2_out, multiplexer_3_out, multiplexer_4_out, multiplexer_5_out,
       multiplexer_6_out, multiplexer_7_out, multiplexer_8_out, multiplexer_9_out, multiplexer_10_out;

  D_Flip_Flop d_ff_1 (.clk(CLOCK), .D(multiplexer_1_out), .Q(\Saída [0]), .reset(Clear));  // open: Qn, preset, en
  Multiplexer #(.enable("false")) multiplexer_1 (
    .in0(\Saída [0]), .in1(Entrada[0]), .out(multiplexer_1_out), .sel(Load));
  D_Flip_Flop d_ff_2 (.clk(CLOCK), .D(multiplexer_2_out), .Q(\Saída [1]), .reset(Clear));  // open: Qn, preset, en
  Multiplexer #(.enable("false")) multiplexer_2 (
    .in0(\Saída [1]), .in1(Entrada[1]), .out(multiplexer_2_out), .sel(Load));
  D_Flip_Flop d_ff_3 (.clk(CLOCK), .D(multiplexer_3_out), .Q(\Saída [2]), .reset(Clear));  // open: Qn, preset, en
  Multiplexer #(.enable("false")) multiplexer_3 (
    .in0(\Saída [2]), .in1(Entrada[2]), .out(multiplexer_3_out), .sel(Load));
  D_Flip_Flop d_ff_4 (.clk(CLOCK), .D(multiplexer_4_out), .Q(\Saída [3]), .reset(Clear));  // open: Qn, preset, en
  Multiplexer #(.enable("false")) multiplexer_4 (
    .in0(\Saída [3]), .in1(Entrada[3]), .out(multiplexer_4_out), .sel(Load));
  D_Flip_Flop d_ff_5 (.clk(CLOCK), .D(multiplexer_5_out), .Q(\Saída [4]), .reset(Clear));  // open: Qn, preset, en
  Multiplexer #(.enable("false")) multiplexer_5 (
    .in0(\Saída [4]), .in1(Entrada[4]), .out(multiplexer_5_out), .sel(Load));
  D_Flip_Flop d_ff_6 (.clk(CLOCK), .D(multiplexer_6_out), .Q(\Saída [5]), .reset(Clear));  // open: Qn, preset, en
  Multiplexer #(.enable("false")) multiplexer_6 (
    .in0(\Saída [5]), .in1(Entrada[5]), .out(multiplexer_6_out), .sel(Load));
  D_Flip_Flop d_ff_7 (.clk(CLOCK), .D(multiplexer_7_out), .Q(\Saída [6]), .reset(Clear));  // open: Qn, preset, en
  Multiplexer #(.enable("false")) multiplexer_7 (
    .in0(\Saída [6]), .in1(Entrada[6]), .out(multiplexer_7_out), .sel(Load));
  D_Flip_Flop d_ff_8 (.clk(CLOCK), .D(multiplexer_8_out), .Q(\Saída [7]), .reset(Clear));  // open: Qn, preset, en
  Multiplexer #(.enable("false")) multiplexer_8 (
    .in0(\Saída [7]), .in1(Entrada[7]), .out(multiplexer_8_out), .sel(Load));
  D_Flip_Flop d_ff_9 (.D(multiplexer_9_out), .Q(\Saída [8]), .reset(Clear));  // open: clk, Qn, preset, en
  Multiplexer #(.enable("false")) multiplexer_9 (
    .in0(\Saída [8]), .in1(Entrada[8]), .out(multiplexer_9_out), .sel(Load));
  D_Flip_Flop d_ff_10 (.clk(CLOCK), .D(multiplexer_10_out), .Q(\Saída [9]), .reset(Clear));  // open: Qn, preset, en
  Multiplexer #(.enable("false")) multiplexer_10 (
    .in0(\Saída [9]), .in1(Entrada[9]), .out(multiplexer_10_out), .sel(Load));

  // Notes on the sheet:
  //   LSB
  //   MSB
endmodule

module _001 (
  input  CLK,
  input  [5:0] CX,
  input  [2:0] ESTADO,
  input  CLR,
  input  [9:0] VALOR
);

  wire and_1_out, comparator_1_gt, comparator_2_eq, comparator_2_gt, comparator_2_lt;
  wire [5:0] adder_1_out, memoria_6bits_1_out_5, memoria_6bits_2_out_5;
  wire [9:0] adder_2_out, memoria_10bits_1_output, memoria_10bits_2_output;

  and and_1 (and_1_out, ESTADO[0], ~ESTADO[1], ~ESTADO[2]);  // AND_Gate
  // Probe on VALOR
  Memoria_6bits memoria_6bits_1 (.CLK(CLK), .out_5(memoria_6bits_1_out_5), .in_4(CX), .in_3(and_1_out));  // open: CLR
  Memoria_6bits memoria_6bits_2 (
    .CLK(CLK), .out_5(memoria_6bits_2_out_5), .in_4(adder_1_out), .CLR(CLR), .in_3(and_1_out));
  Memoria_10bits memoria_10bits_1 (
    .CLK(CLK), .OUTPUT(memoria_10bits_1_output), .Input(VALOR), .CLR(CLR), .EN(comparator_1_gt));
  // Probe on memoria_10bits_2_output
  Memoria_10bits memoria_10bits_2 (
    .CLK(CLK), .OUTPUT(memoria_10bits_2_output), .Input(adder_2_out), .CLR(CLR), .EN(comparator_1_gt));
  Comparator #(.width(6)) comparator_1 (
    .a(memoria_6bits_1_out_5), .b(memoria_6bits_2_out_5), .gt(comparator_1_gt));  // open: eq, lt
  // Probe on memoria_6bits_2_out_5
  Adder #(.width(6)) adder_1 (.a(memoria_6bits_2_out_5), .b(6'b000001), .out(adder_1_out));  // open: cin, cout
  Comparator #(.width(10)) comparator_2 (
    .a(memoria_10bits_1_output), .b(memoria_10bits_2_output), .gt(comparator_2_gt), .eq(comparator_2_eq),
    .lt(comparator_2_lt));
  Adder #(.width(10)) adder_2 (.a(memoria_10bits_2_output), .b(10'h64), .out(adder_2_out));  // open: cin, cout

  // Notes on the sheet:
  //   Quant_CX
  //   Quant_CX_TEMP
  //   VALOR
  //   VALOR_TEMP
  //   MENOR
endmodule
