// Logisim project Memoria.circ as structural Verilog
module _1_bit (
  input  CLK,
  input  LER,
  input  D,
  input  EN,
  input  CLR,
  output Saida
);

  wire d_ff_1_q, multiplexer_1_out, pull_resistor_1_node;

  Multiplexer #(.enable("false")) multiplexer_1 (.in0(d_ff_1_q), .in1(D), .out(multiplexer_1_out), .sel(EN));
  D_Flip_Flop d_ff_1 (.clk(CLK), .D(multiplexer_1_out), .Q(d_ff_1_q), .reset(CLR));  // open: Qn, preset, en
  Pull_Resistor pull_resistor_1 (.node(pull_resistor_1_node));
  Multiplexer #(.enable("false")) multiplexer_2 (.in0(pull_resistor_1_node), .in1(d_ff_1_q), .out(Saida), .sel(LER));
endmodule

module _13_bits (
  input  CLK,
  input  wd_en,
  input  CLR,
  input  rd_en,
  input  [12:0] wd_data,
  output [12:0] SAIDA
);

  _1_bit u_1_bit_1 (.CLK(CLK), .D(wd_data[0]), .EN(wd_en), .CLR(CLR), .Saida(SAIDA[0]), .LER(rd_en));
  _1_bit u_1_bit_2 (.CLK(CLK), .D(wd_data[1]), .EN(wd_en), .CLR(CLR), .Saida(SAIDA[1]), .LER(rd_en));
  _1_bit u_1_bit_3 (.CLK(CLK), .D(wd_data[2]), .EN(wd_en), .CLR(CLR), .Saida(SAIDA[2]), .LER(rd_en));
  _1_bit u_1_bit_4 (.CLK(CLK), .D(wd_data[3]), .EN(wd_en), .CLR(CLR), .Saida(SAIDA[3]), .LER(rd_en));
  _1_bit u_1_bit_5 (.CLK(CLK), .D(wd_data[4]), .EN(wd_en), .CLR(CLR), .Saida(SAIDA[4]), .LER(rd_en));
  _1_bit u_1_bit_6 (.CLK(CLK), .D(wd_data[5]), .EN(wd_en), .CLR(CLR), .Saida(SAIDA[5]), .LER(rd_en));
  _1_bit u_1_bit_7 (.CLK(CLK), .D(wd_data[6]), .EN(wd_en), .CLR(CLR), .Saida(SAIDA[6]), .LER(rd_en));
  _1_bit u_1_bit_8 (.CLK(CLK), .D(wd_data[7]), .EN(wd_en), .CLR(CLR), .Saida(SAIDA[7]), .LER(rd_en));
  _1_bit u_1_bit_9 (.CLK(CLK), .D(wd_data[8]), .EN(wd_en), .CLR(CLR), .Saida(SAIDA[8]), .LER(rd_en));
  _1_bit u_1_bit_10 (.CLK(CLK), .D(wd_data[9]), .EN(wd_en), .CLR(CLR), .Saida(SAIDA[9]), .LER(rd_en));
  _1_bit u_1_bit_11 (.CLK(CLK), .D(wd_data[10]), .EN(wd_en), .CLR(CLR), .Saida(SAIDA[10]), .LER(rd_en));
  _1_bit u_1_bit_12 (.CLK(CLK), .D(wd_data[11]), .EN(wd_en), .CLR(CLR), .Saida(SAIDA[11]), .LER(rd_en));
  _1_bit u_1_bit_13 (.CLK(CLK), .D(wd_data[12]), .EN(wd_en), .CLR(CLR), .Saida(SAIDA[12]), .LER(rd_en));

  // Other names for the same wires on the sheet: I0 = wd_data[0]; I1 = wd_data[1]; I2 = wd_data[2]; I3 = wd_data[3];
  //   I4 = wd_data[4]; I5 = wd_data[5]; I6 = wd_data[6]; I7 = wd_data[7]; I8 = wd_data[8]; I9 = wd_data[9];
  //   I10 = wd_data[10]; I11 = wd_data[11]; I12 = wd_data[12]
endmodule

module Conjunto_4Palavras (
  input  CLK,
  input  CLR,
  input  wd_addr_01,
  input  wd_addr_02,
  input  wd_addr_03,
  input  wd_addr_04,
  input  rd_addr_01,
  input  rd_addr_02,
  input  rd_addr_03,
  input  rd_addr_04,
  input  [12:0] wd_data,
  output [12:0] rd_data,
  output [12:0] rd_data_2,
  output [12:0] rd_data_3,
  output [12:0] rd_data_4
);

  _13_bits u_13_bits_1 (
    .CLK(CLK), .wd_en(wd_addr_01), .CLR(CLR), .rd_en(rd_addr_01), .SAIDA(rd_data), .wd_data(wd_data));
  _13_bits u_13_bits_2 (
    .CLK(CLK), .wd_en(wd_addr_02), .CLR(CLR), .rd_en(rd_addr_02), .SAIDA(rd_data_2), .wd_data(wd_data));
  _13_bits u_13_bits_3 (
    .CLK(CLK), .wd_en(wd_addr_03), .CLR(CLR), .rd_en(rd_addr_03), .SAIDA(rd_data_3), .wd_data(wd_data));
  _13_bits u_13_bits_4 (
    .CLK(CLK), .wd_en(wd_addr_04), .CLR(CLR), .rd_en(rd_addr_04), .SAIDA(rd_data_4), .wd_data(wd_data));
endmodule

module Circuito_Memoria (
  input  [12:0] w_data,
  input  CLK,
  input  CLR,
  input  wd,
  input  [3:0] wd_addr,
  input  rd,
  input  [3:0] rd_addr,
  output [12:0] rd_data
);

  wire r0, r1, r2, r3, r4, r5, r6, r7, r8, r9, r10, r11, r12, r13, r14, r15, w0, w1, w2, w3, w4, w5, w6, w7,
       w8, w9, w10, w11, w12, w13, w14, w15;
  wire [12:0] Q1, Q2, Q3, Q4, Q5, Q6, Q7, Q8, Q9, Q10, Q11, Q12, Q13, Q14, Q15, Q16;

  Decoder #(.select(4)) decoder_1 (
    .out0(w0), .out1(w1), .out2(w2), .out3(w3), .out4(w4), .out5(w5), .out6(w6), .out7(w7), .out8(w8),
    .out9(w9), .out10(w10), .out11(w11), .out12(w12), .out13(w13), .out14(w14), .out15(w15), .sel(wd_addr),
    .en(wd));
  Conjunto_4Palavras conjunto_4palavras_1 (
    .CLK(CLK), .wd_data(w_data), .rd_data(Q1), .rd_data_2(Q2), .rd_data_3(Q3), .rd_data_4(Q4),
    .wd_addr_01(w0), .wd_addr_02(w1), .wd_addr_03(w2), .wd_addr_04(w3), .rd_addr_01(r0), .rd_addr_02(r1),
    .rd_addr_03(r2), .rd_addr_04(r3), .CLR(CLR));
  Conjunto_4Palavras conjunto_4palavras_2 (
    .CLK(CLK), .wd_data(w_data), .rd_data(Q5), .rd_data_2(Q6), .rd_data_3(Q7), .rd_data_4(Q8),
    .wd_addr_01(w4), .wd_addr_02(w5), .wd_addr_03(w6), .wd_addr_04(w7), .rd_addr_01(r4), .rd_addr_02(r5),
    .rd_addr_03(r6), .rd_addr_04(r7), .CLR(CLR));
  Conjunto_4Palavras conjunto_4palavras_3 (
    .CLK(CLK), .wd_data(w_data), .rd_data(Q9), .rd_data_2(Q10), .rd_data_3(Q11), .rd_data_4(Q12),
    .wd_addr_01(w8), .wd_addr_02(w9), .wd_addr_03(w10), .wd_addr_04(w11), .rd_addr_01(r8), .rd_addr_02(r9),
    .rd_addr_03(r10), .rd_addr_04(r11), .CLR(CLR));
  Conjunto_4Palavras conjunto_4palavras_4 (
    .CLK(CLK), .wd_data(w_data), .rd_data(Q13), .rd_data_2(Q14), .rd_data_3(Q15), .rd_data_4(Q16),
    .wd_addr_01(w12), .wd_addr_02(w13), .wd_addr_03(w14), .wd_addr_04(w15), .rd_addr_01(r12),
    .rd_addr_02(r13), .rd_addr_03(r14), .rd_addr_04(r15), .CLR(CLR));
  Multiplexer #(.select(4), .width(13), .enable("false")) multiplexer_1 (
    .in0(Q1), .in1(Q2), .in2(Q3), .in3(Q4), .in4(Q5), .in5(Q6), .in6(Q7), .in7(Q8), .in8(Q9), .in9(Q10),
    .in10(Q11), .in11(Q12), .in12(Q13), .in13(Q14), .in14(Q15), .in15(Q16), .out(rd_data), .sel(rd_addr));
  Decoder #(.select(4)) decoder_2 (
    .out0(r0), .out1(r1), .out2(r2), .out3(r3), .out4(r4), .out5(r5), .out6(r6), .out7(r7), .out8(r8),
    .out9(r9), .out10(r10), .out11(r11), .out12(r12), .out13(r13), .out14(r14), .out15(r15), .sel(rd_addr),
    .en(rd));
endmodule

module Estados (
  input  A2,
  input  A1,
  input  A0,
  input  WR_FU,
  input  RESET,
  input  RD_EM,
  input  WR,
  input  RD,
  output B2,
  output B1,
  output B0,
  output full,
  output empty,
  output clr
);

  wire and_4_out, and_5_out, and_6_out, and_7_out, and_8_out, and_9_out, and_10_out, and_11_out, and_12_out,
       and_13_out, and_14_out, and_15_out, and_16_out, and_17_out, and_18_out, and_19_out, not_1_out,
       not_2_out, not_3_out, not_4_out, not_5_out, not_6_out, not_7_out, not_8_out, not_9_out, not_10_out,
       not_11_out, not_12_out, not_13_out, not_14_out, not_15_out, not_16_out, not_17_out, not_18_out,
       not_19_out, not_20_out, not_21_out, not_22_out, not_23_out, not_24_out, not_25_out, not_26_out,
       not_27_out, not_28_out, not_29_out, not_30_out, not_31_out, not_32_out, not_33_out, not_34_out,
       not_35_out, not_36_out, not_37_out, not_38_out, not_39_out, not_40_out, not_41_out, not_42_out,
       not_43_out, not_44_out, not_45_out, not_46_out, not_47_out, not_48_out, not_49_out, not_50_out,
       not_51_out, not_52_out, not_53_out, not_54_out, not_55_out, not_56_out, not_57_out, not_58_out,
       not_59_out;

  not not_1 (not_1_out, A2);
  not not_2 (not_2_out, A0);
  not not_3 (not_3_out, WR_FU);
  not not_4 (not_4_out, RESET);
  not not_5 (not_5_out, A2);
  not not_6 (not_6_out, A0);
  not not_7 (not_7_out, RESET);
  not not_8 (not_8_out, A2);
  not not_9 (not_9_out, RD_EM);
  not not_10 (not_10_out, RESET);
  not not_11 (not_11_out, A1);
  not not_12 (not_12_out, A0);
  not not_13 (not_13_out, WR);
  not not_14 (not_14_out, RD);
  not not_15 (not_15_out, RESET);
  not not_16 (not_16_out, A1);
  not not_17 (not_17_out, RD);
  not not_18 (not_18_out, RESET);
  not not_19 (not_19_out, A2);
  not not_20 (not_20_out, A1);
  not not_21 (not_21_out, RD);
  not not_22 (not_22_out, RESET);
  not not_23 (not_23_out, A1);
  not not_24 (not_24_out, A0);
  not not_25 (not_25_out, RESET);
  not not_26 (not_26_out, A1);
  not not_27 (not_27_out, A0);
  not not_28 (not_28_out, RESET);
  not not_29 (not_29_out, A1);
  not not_30 (not_30_out, WR);
  not not_31 (not_31_out, RESET);
  not not_32 (not_32_out, A2);
  not not_33 (not_33_out, A1);
  not not_34 (not_34_out, A0);
  not not_35 (not_35_out, RESET);
  not not_36 (not_36_out, A2);
  not not_37 (not_37_out, A1);
  not not_38 (not_38_out, WR);
  not not_39 (not_39_out, RESET);
  not not_40 (not_40_out, A2);
  not not_41 (not_41_out, A0);
  not not_42 (not_42_out, RESET);
  not not_43 (not_43_out, A2);
  not not_44 (not_44_out, RESET);
  not not_45 (not_45_out, A1);
  not not_46 (not_46_out, A0);
  not not_47 (not_47_out, RESET);
  not not_48 (not_48_out, A1);
  not not_49 (not_49_out, WR);
  not not_50 (not_50_out, RESET);
  not not_51 (not_51_out, A1);
  not not_52 (not_52_out, RD);
  not not_53 (not_53_out, RESET);
  and and_1 (full, A2, not_54_out, A0);
  not not_54 (not_54_out, A1);
  not not_55 (not_55_out, A2);
  not not_56 (not_56_out, A1);
  and and_2 (empty, not_55_out, not_56_out, A0);
  not not_57 (not_57_out, A2);
  and and_3 (clr, not_57_out, not_58_out, not_59_out);
  not not_58 (not_58_out, A1);
  not not_59 (not_59_out, A0);
  and and_4 (and_4_out, not_1_out, A1, not_2_out, not_3_out, not_4_out);
  and and_5 (and_5_out, not_5_out, A1, not_6_out, WR_FU, not_7_out);
  and and_6 (and_6_out, not_8_out, A1, A0, not_9_out, not_10_out);
  and and_7 (and_7_out, A2, not_11_out, not_12_out, not_13_out, not_14_out, not_15_out);
  and and_8 (and_8_out, A2, not_16_out, A0, not_17_out, not_18_out);
  and and_9 (and_9_out, not_19_out, not_20_out, A0, WR, not_21_out, not_22_out);
  and and_10 (and_10_out, A2, not_23_out, not_24_out, WR, not_25_out);
  and and_11 (and_11_out, A2, not_26_out, not_27_out, RD, not_28_out);
  and and_12 (and_12_out, A2, not_29_out, A0, not_30_out, RD, not_31_out);
  and and_13 (and_13_out, not_32_out, not_33_out, not_34_out, not_35_out);
  and and_14 (and_14_out, not_36_out, not_37_out, A0, not_38_out, not_39_out);
  and and_15 (and_15_out, not_40_out, A1, not_41_out, WR_FU, not_42_out);
  and and_16 (and_16_out, not_43_out, A1, A0, RD_EM, not_44_out);
  and and_17 (and_17_out, A2, not_45_out, not_46_out, RD, not_47_out);
  and and_18 (and_18_out, A2, not_48_out, A0, not_49_out, RD, not_50_out);
  and and_19 (and_19_out, A2, not_51_out, A0, not_52_out, not_53_out);
  or or_1 (B2, and_4_out, and_5_out, and_6_out, and_7_out, and_8_out);
  or or_2 (B1, and_9_out, and_10_out, and_11_out, and_12_out);
  or or_3 (B0, and_13_out, and_14_out, and_15_out, and_16_out, and_17_out, and_18_out, and_19_out);
endmodule

module Cont_WR (
  input  clk,
  input  clear,
  input  in_3,
  input  in_4,
  input  in_5,
  output s0,
  output s1,
  output s2,
  output s3
);

  wire and_1_out, and_2_out, and_3_out;

  and and_1 (and_1_out, ~in_3, in_4, ~in_5);  // AND_Gate
  J_K_Flip_Flop j_k_ff_1 (.J(1'b1), .clk(clk), .K(1'b1), .Q(s0), .en(and_1_out), .reset(clear));  // open: Qn, preset
  J_K_Flip_Flop j_k_ff_2 (.J(s0), .clk(clk), .K(s0), .Q(s1), .en(and_1_out), .reset(clear));  // open: Qn, preset
  and and_2 (and_2_out, s0, s1);
  J_K_Flip_Flop j_k_ff_3 (
    .J(and_2_out), .clk(clk), .K(and_2_out), .Q(s2), .en(and_1_out), .reset(clear));  // open: Qn, preset
  and and_3 (and_3_out, and_2_out, s2);
  J_K_Flip_Flop j_k_ff_4 (
    .J(and_3_out), .clk(clk), .K(and_3_out), .Q(s3), .en(and_1_out), .reset(clear));  // open: Qn, preset
endmodule

module cont_RD (
  input  clk,
  input  clear,
  input  in_3,
  input  in_4,
  input  in_5,
  output s0,
  output s1,
  output s2,
  output s3
);

  wire and_1_out, and_2_out, and_3_out;

  and and_1 (and_1_out, ~in_3, in_4, in_5);  // AND_Gate
  J_K_Flip_Flop j_k_ff_1 (.J(1'b1), .clk(clk), .K(1'b1), .Q(s0), .en(and_1_out), .reset(clear));  // open: Qn, preset
  J_K_Flip_Flop j_k_ff_2 (.J(s0), .clk(clk), .K(s0), .Q(s1), .en(and_1_out), .reset(clear));  // open: Qn, preset
  and and_2 (and_2_out, s0, s1);
  J_K_Flip_Flop j_k_ff_3 (
    .J(and_2_out), .clk(clk), .K(and_2_out), .Q(s2), .en(and_1_out), .reset(clear));  // open: Qn, preset
  and and_3 (and_3_out, and_2_out, s2);
  J_K_Flip_Flop j_k_ff_4 (
    .J(and_3_out), .clk(clk), .K(and_3_out), .Q(s3), .en(and_1_out), .reset(clear));  // open: Qn, preset
endmodule

module comparador_4_bits (
  input  [3:0] A,
  input  [3:0] B,
  output A_B,
  output A_B_2,
  output A_B_3
);

  Comparator #(.width(4)) comparator_1 (.a(A), .b(B), .gt(A_B), .eq(A_B_2), .lt(A_B_3));
endmodule
