// Logisim project Deslocador.circ as structural Verilog: 3 circuits, main circuit main
module main (
  input  in_1,
  input  [2:0] in_2,
  input  in_3,
  output [7:0] out_4,
  output [7:0] out_5
);

  Shifter shifter_1 (
    .s0(in_2[0]), .E(in_1), .s1(in_2[1]), .s2(in_2[2]), .I7(1'b1), .I6(1'b1), .I5(1'b1), .I4(1'b1),
    .I3(1'b1), .I2(1'b1), .I1(1'b1), .I0(1'b1), .out_14(out_4[7]), .out_15(out_4[6]), .out_16(out_4[5]),
    .out_17(out_4[4]), .out_18(out_4[3]), .out_19(out_4[2]), .out_20(out_4[1]), .out_21(out_4[0]));  // open: Z, c
  Shifte shifte_1 (
    .s0(in_2[0]), .E(in_3), .s1(in_2[1]), .s2(in_2[2]), .I7(1'b1), .I6(1'b1), .I5(1'b1), .I4(1'b1),
    .I3(1'b1), .I2(1'b1), .I1(1'b1), .I0(1'b1), .out_13(out_5[7]), .out_14(out_5[6]), .out_15(out_5[5]),
    .out_16(out_5[4]), .out_17(out_5[3]), .out_18(out_5[2]), .out_19(out_5[1]), .out_20(out_5[0]));  // open: Z
endmodule

module Shifter (
  input  I7,
  input  I6,
  input  I5,
  input  I4,
  input  I3,
  input  I2,
  input  I1,
  input  I0,
  input  s0,
  input  E,
  input  s1,
  input  s2,
  output c,
  output out_14,
  output out_15,
  output out_16,
  output out_17,
  output out_18,
  output out_19,
  output out_20,
  output out_21,
  output Z
);

  wire multiplexer_1_out, multiplexer_2_out, multiplexer_4_out, multiplexer_5_out, multiplexer_7_out,
       multiplexer_8_out, multiplexer_10_out, multiplexer_11_out, multiplexer_13_out, multiplexer_14_out,
       multiplexer_16_out, multiplexer_17_out, multiplexer_19_out, multiplexer_20_out, multiplexer_22_out,
       multiplexer_23_out, not_1_out, or_1_out;

  not not_1 (not_1_out, E);
  Multiplexer multiplexer_1 (.in0(I7), .in1(I6), .out(multiplexer_1_out), .sel(s0), .en(not_1_out));
  Multiplexer multiplexer_2 (
    .in0(multiplexer_1_out), .in1(multiplexer_7_out), .out(multiplexer_2_out), .sel(s1), .en(not_1_out));
  Multiplexer multiplexer_3 (.in0(multiplexer_2_out), .in1(multiplexer_14_out), .out(c), .sel(s2), .en(not_1_out));
  Multiplexer multiplexer_4 (.in0(I6), .in1(I5), .out(multiplexer_4_out), .sel(s0), .en(not_1_out));
  Multiplexer multiplexer_5 (
    .in0(multiplexer_4_out), .in1(multiplexer_10_out), .out(multiplexer_5_out), .sel(s1), .en(not_1_out));
  Multiplexer multiplexer_6 (.in0(multiplexer_5_out), .in1(multiplexer_17_out), .out(out_15), .sel(s2), .en(not_1_out));
  Multiplexer multiplexer_7 (.in0(I5), .in1(I4), .out(multiplexer_7_out), .sel(s0), .en(not_1_out));
  Multiplexer multiplexer_8 (
    .in0(multiplexer_7_out), .in1(multiplexer_13_out), .out(multiplexer_8_out), .sel(s1), .en(not_1_out));
  Multiplexer multiplexer_9 (.in0(multiplexer_8_out), .in1(multiplexer_20_out), .out(out_16), .sel(s2), .en(not_1_out));
  Multiplexer multiplexer_10 (.in0(I4), .in1(I3), .out(multiplexer_10_out), .sel(s0), .en(not_1_out));
  Multiplexer multiplexer_11 (
    .in0(multiplexer_10_out), .in1(multiplexer_16_out), .out(multiplexer_11_out), .sel(s1), .en(not_1_out));
  Multiplexer multiplexer_12 (
    .in0(multiplexer_11_out), .in1(multiplexer_23_out), .out(out_17), .sel(s2), .en(not_1_out));
  Multiplexer multiplexer_13 (.in0(I3), .in1(I2), .out(multiplexer_13_out), .sel(s0), .en(not_1_out));
  Multiplexer multiplexer_14 (
    .in0(multiplexer_13_out), .in1(multiplexer_19_out), .out(multiplexer_14_out), .sel(s1), .en(not_1_out));
  Multiplexer multiplexer_15 (.in0(multiplexer_14_out), .in1(1'b0), .out(out_18), .sel(s2), .en(not_1_out));
  or or_1 (or_1_out, c, out_15, out_16, out_17, out_18, out_19, out_20, out_21);
  Multiplexer multiplexer_16 (.in0(I2), .in1(I1), .out(multiplexer_16_out), .sel(s0), .en(not_1_out));
  Multiplexer multiplexer_17 (
    .in0(multiplexer_16_out), .in1(multiplexer_22_out), .out(multiplexer_17_out), .sel(s1), .en(not_1_out));
  Multiplexer multiplexer_18 (.in0(multiplexer_17_out), .in1(1'b0), .out(out_19), .sel(s2), .en(not_1_out));
  not not_2 (Z, or_1_out);
  Multiplexer multiplexer_19 (.in0(I1), .in1(I0), .out(multiplexer_19_out), .sel(s0), .en(not_1_out));
  Multiplexer multiplexer_20 (.in0(multiplexer_19_out), .in1(1'b0), .out(multiplexer_20_out), .sel(s1), .en(not_1_out));
  Multiplexer multiplexer_21 (.in0(multiplexer_20_out), .in1(1'b0), .out(out_20), .sel(s2), .en(not_1_out));
  Multiplexer multiplexer_22 (.in0(I0), .in1(1'b0), .out(multiplexer_22_out), .sel(s0), .en(not_1_out));
  Multiplexer multiplexer_23 (.in0(multiplexer_22_out), .in1(1'b0), .out(multiplexer_23_out), .sel(s1), .en(not_1_out));
  Multiplexer multiplexer_24 (.in0(multiplexer_23_out), .in1(1'b0), .out(out_21), .sel(s2), .en(not_1_out));

  assign out_14 = c;

  // Other names for the same wires on the sheet: q0 = out_21; q1 = out_20; q2 = out_19; q3 = out_18; q4 = out_17;
  //   q5 = out_16; q6 = out_15; q7 = c
endmodule

module Shifte (
  input  I7,
  input  I6,
  input  I5,
  input  I4,
  input  I3,
  input  I2,
  input  I1,
  input  I0,
  input  s0,
  input  E,
  input  s1,
  input  s2,
  output out_13,
  output out_14,
  output out_15,
  output out_16,
  output out_17,
  output out_18,
  output out_19,
  output out_20,
  output Z
);

  wire multiplexer_1_out, multiplexer_2_out, multiplexer_4_out, multiplexer_5_out, multiplexer_7_out,
       multiplexer_8_out, multiplexer_10_out, multiplexer_11_out, multiplexer_13_out, multiplexer_14_out,
       multiplexer_16_out, multiplexer_17_out, multiplexer_19_out, multiplexer_20_out, multiplexer_22_out,
       multiplexer_23_out, not_1_out, or_1_out;

  not not_1 (not_1_out, E);
  Multiplexer multiplexer_1 (.in0(I7), .in1(1'b0), .out(multiplexer_1_out), .sel(s0), .en(not_1_out));
  Multiplexer multiplexer_2 (.in0(multiplexer_1_out), .in1(1'b0), .out(multiplexer_2_out), .sel(s1), .en(not_1_out));
  Multiplexer multiplexer_3 (.in0(multiplexer_2_out), .in1(1'b0), .out(out_13), .sel(s2), .en(not_1_out));
  Multiplexer multiplexer_4 (.in0(I6), .in1(I7), .out(multiplexer_4_out), .sel(s0), .en(not_1_out));
  Multiplexer multiplexer_5 (.in0(multiplexer_4_out), .in1(1'b0), .out(multiplexer_5_out), .sel(s1), .en(not_1_out));
  Multiplexer multiplexer_6 (.in0(multiplexer_5_out), .in1(1'b0), .out(out_14), .sel(s2), .en(not_1_out));
  Multiplexer multiplexer_7 (.in0(I5), .in1(I6), .out(multiplexer_7_out), .sel(s0), .en(not_1_out));
  Multiplexer multiplexer_8 (
    .in0(multiplexer_7_out), .in1(multiplexer_1_out), .out(multiplexer_8_out), .sel(s1), .en(not_1_out));
  Multiplexer multiplexer_9 (.in0(multiplexer_8_out), .in1(1'b0), .out(out_15), .sel(s2), .en(not_1_out));
  Multiplexer multiplexer_10 (.in0(I4), .in1(I5), .out(multiplexer_10_out), .sel(s0), .en(not_1_out));
  Multiplexer multiplexer_11 (
    .in0(multiplexer_10_out), .in1(multiplexer_4_out), .out(multiplexer_11_out), .sel(s1), .en(not_1_out));
  Multiplexer multiplexer_12 (.in0(multiplexer_11_out), .in1(1'b0), .out(out_16), .sel(s2), .en(not_1_out));
  Multiplexer multiplexer_13 (.in0(I3), .in1(I4), .out(multiplexer_13_out), .sel(s0), .en(not_1_out));
  Multiplexer multiplexer_14 (
    .in0(multiplexer_13_out), .in1(multiplexer_7_out), .out(multiplexer_14_out), .sel(s1), .en(not_1_out));
  Multiplexer multiplexer_15 (
    .in0(multiplexer_14_out), .in1(multiplexer_2_out), .out(out_17), .sel(s2), .en(not_1_out));
  or or_1 (or_1_out, out_13, out_14, out_15, out_16, out_17, out_18, out_19, out_20);
  Multiplexer multiplexer_16 (.in0(I2), .in1(I3), .out(multiplexer_16_out), .sel(s0), .en(not_1_out));
  Multiplexer multiplexer_17 (
    .in0(multiplexer_16_out), .in1(multiplexer_10_out), .out(multiplexer_17_out), .sel(s1), .en(not_1_out));
  Multiplexer multiplexer_18 (
    .in0(multiplexer_17_out), .in1(multiplexer_5_out), .out(out_18), .sel(s2), .en(not_1_out));
  not not_2 (Z, or_1_out);
  Multiplexer multiplexer_19 (.in0(I1), .in1(I2), .out(multiplexer_19_out), .sel(s0), .en(not_1_out));
  Multiplexer multiplexer_20 (
    .in0(multiplexer_19_out), .in1(multiplexer_13_out), .out(multiplexer_20_out), .sel(s1), .en(not_1_out));
  Multiplexer multiplexer_21 (
    .in0(multiplexer_20_out), .in1(multiplexer_8_out), .out(out_19), .sel(s2), .en(not_1_out));
  Multiplexer multiplexer_22 (.in0(I0), .in1(I1), .out(multiplexer_22_out), .sel(s0), .en(not_1_out));
  Multiplexer multiplexer_23 (
    .in0(multiplexer_22_out), .in1(multiplexer_16_out), .out(multiplexer_23_out), .sel(s1), .en(not_1_out));
  Multiplexer multiplexer_24 (
    .in0(multiplexer_23_out), .in1(multiplexer_11_out), .out(out_20), .sel(s2), .en(not_1_out));

  // Other names for the same wires on the sheet: q0 = out_20; q1 = out_19; q2 = out_18; q3 = out_17; q4 = out_16;
  //   q5 = out_15; q6 = out_14; q7 = out_13
endmodule
