// Logisim project Multiplicador.circ as structural Verilog
module Multiplicador_8bits (
  input  [7:0] in_1,
  input  [7:0] in_2,
  output out_3,
  output [7:0] out_4
);

  wire add16_1_out_5, add16_2_out_5, add16_3_out_5, add16_4_out_5, add16_5_out_5, add16_6_out_5,
       pull_resistor_1_node;
  wire [15:0] add16_1_out_4, add16_2_out_4, add16_3_out_4, add16_4_out_4, add16_5_out_4, add16_6_out_4, m0,
       m1;
  wire [15:1] m2;
  wire [15:2] m3;
  wire [15:3] m4;
  wire [15:4] m5;
  wire [15:5] m6;
  wire [15:6] m7;
  wire [15:15] add16_7_out_4;

  Pull_Resistor pull_resistor_1 (.node(pull_resistor_1_node));
  ADD16 add16_1 (
    .in_2(pull_resistor_1_node), .in_1({{8{m0[15]}}, m0[7:0]}), .in_3({{7{m1[15]}}, m1[8:0]}),
    .out_4(add16_1_out_4), .out_5(add16_1_out_5));
  ADD16 add16_2 (
    .in_2(add16_1_out_5), .in_1(add16_1_out_4), .in_3({{6{m2[15]}}, m2[9:1], m2[1]}), .out_4(add16_2_out_4),
    .out_5(add16_2_out_5));
  ADD16 add16_3 (
    .in_2(add16_2_out_5), .in_1(add16_2_out_4), .in_3({{5{m3[15]}}, m3[10:2], {2{m3[2]}}}),
    .out_4(add16_3_out_4), .out_5(add16_3_out_5));
  ADD16 add16_4 (
    .in_2(add16_3_out_5), .in_1(add16_3_out_4), .in_3({{4{m4[15]}}, m4[11:3], {3{m4[3]}}}),
    .out_4(add16_4_out_4), .out_5(add16_4_out_5));
  ADD16 add16_5 (
    .in_2(add16_4_out_5), .in_1(add16_4_out_4), .in_3({{3{m5[15]}}, m5[12:4], {4{m5[4]}}}),
    .out_4(add16_5_out_4), .out_5(add16_5_out_5));
  ADD16 add16_6 (
    .in_2(add16_5_out_5), .in_1(add16_5_out_4), .in_3({{2{m6[15]}}, m6[13:5], {5{m6[5]}}}),
    .out_4(add16_6_out_4), .out_5(add16_6_out_5));
  ADD16 add16_7 (
    .in_2(add16_6_out_5), .in_1(add16_6_out_4), .in_3({m7, {6{m7[6]}}}),
    .out_4({{8{add16_7_out_4[15]}}, out_4}), .out_5(out_3));
  Pull_Resistor pull_resistor_2 (.node(add16_7_out_4[15]));
  and and_1 (m0[7], in_1[7], in_2[0]);
  and and_2 (m1[8], in_1[7], in_2[1]);
  and and_3 (m2[9], in_1[7], in_2[2]);
  and and_4 (m3[10], in_1[7], in_2[3]);
  and and_5 (m4[11], in_1[7], in_2[4]);
  and and_6 (m0[6], in_1[6], in_2[0]);
  and and_7 (m1[7], in_1[6], in_2[1]);
  and and_8 (m2[8], in_1[6], in_2[2]);
  Pull_Resistor pull_resistor_3 (.node(m2[15]));
  and and_9 (m3[9], in_1[6], in_2[3]);
  and and_10 (m4[10], in_1[6], in_2[4]);
  Pull_Resistor pull_resistor_4 (.node(m4[15]));
  and and_11 (m0[5], in_1[5], in_2[0]);
  Pull_Resistor pull_resistor_5 (.node(m0[15]));
  and and_12 (m1[6], in_1[5], in_2[1]);
  Pull_Resistor pull_resistor_6 (.node(m1[15]));
  and and_13 (m2[7], in_1[5], in_2[2]);
  and and_14 (m3[8], in_1[5], in_2[3]);
  Pull_Resistor pull_resistor_7 (.node(m3[15]));
  and and_15 (m4[9], in_1[5], in_2[4]);
  and and_16 (m0[4], in_1[4], in_2[0]);
  and and_17 (m1[5], in_1[4], in_2[1]);
  and and_18 (m2[6], in_1[4], in_2[2]);
  and and_19 (m3[7], in_1[4], in_2[3]);
  and and_20 (m4[8], in_1[4], in_2[4]);
  and and_21 (m0[3], in_1[3], in_2[0]);
  and and_22 (m1[4], in_1[3], in_2[1]);
  Pull_Resistor pull_resistor_8 (.node(m1[0]));
  and and_23 (m2[5], in_1[3], in_2[2]);
  Pull_Resistor pull_resistor_9 (.node(m2[1]));
  and and_24 (m3[6], in_1[3], in_2[3]);
  Pull_Resistor pull_resistor_10 (.node(m3[2]));
  and and_25 (m4[7], in_1[3], in_2[4]);
  Pull_Resistor pull_resistor_11 (.node(m4[3]));
  and and_26 (m0[2], in_1[2], in_2[0]);
  and and_27 (m1[3], in_1[2], in_2[1]);
  and and_28 (m2[4], in_1[2], in_2[2]);
  and and_29 (m3[5], in_1[2], in_2[3]);
  and and_30 (m4[6], in_1[2], in_2[4]);
  and and_31 (m0[1], in_1[1], in_2[0]);
  and and_32 (m1[2], in_1[1], in_2[1]);
  and and_33 (m2[3], in_1[1], in_2[2]);
  and and_34 (m4[5], in_1[1], in_2[4]);
  and and_35 (m0[0], in_1[0], in_2[0]);
  and and_36 (m1[1], in_1[0], in_2[1]);
  and and_37 (m2[2], in_1[0], in_2[2]);
  and and_38 (m3[4], in_1[1], in_2[3]);
  and and_39 (m3[3], in_1[0], in_2[3]);
  and and_40 (m4[4], in_1[0], in_2[4]);
  and and_41 (m5[12], in_1[7], in_2[5]);
  and and_42 (m6[13], in_1[7], in_2[6]);
  and and_43 (m7[14], in_1[7], in_2[7]);
  and and_44 (m5[11], in_1[6], in_2[5]);
  and and_45 (m6[12], in_1[6], in_2[6]);
  and and_46 (m7[13], in_1[6], in_2[7]);
  and and_47 (m5[10], in_1[5], in_2[5]);
  Pull_Resistor pull_resistor_12 (.node(m5[15]));
  and and_48 (m6[11], in_1[5], in_2[6]);
  Pull_Resistor pull_resistor_13 (.node(m6[15]));
  and and_49 (m7[12], in_1[5], in_2[7]);
  Pull_Resistor pull_resistor_14 (.node(m7[15]));
  and and_50 (m5[9], in_1[4], in_2[5]);
  and and_51 (m6[10], in_1[4], in_2[6]);
  and and_52 (m7[11], in_1[4], in_2[7]);
  and and_53 (m5[8], in_1[3], in_2[5]);
  and and_54 (m6[9], in_1[3], in_2[6]);
  Pull_Resistor pull_resistor_15 (.node(m6[5]));
  and and_55 (m7[10], in_1[3], in_2[7]);
  and and_56 (m5[7], in_1[2], in_2[5]);
  Pull_Resistor pull_resistor_16 (.node(m5[4]));
  and and_57 (m6[8], in_1[2], in_2[6]);
  Pull_Resistor pull_resistor_17 (.node(m7[6]));
  and and_58 (m7[9], in_1[2], in_2[7]);
  and and_59 (m5[6], in_1[1], in_2[5]);
  and and_60 (m6[7], in_1[1], in_2[6]);
  and and_61 (m7[8], in_1[1], in_2[7]);
  and and_62 (m5[5], in_1[0], in_2[5]);
  and and_63 (m6[6], in_1[0], in_2[6]);
  and and_64 (m7[7], in_1[0], in_2[7]);

  // Other names for the same wires on the sheet: a0 = in_1[0]; a1 = in_1[1]; a2 = in_1[2]; a3 = in_1[3]; a4 = in_1[4];
  //   a5 = in_1[5]; a6 = in_1[6]; a7 = in_1[7]; b0 = in_2[0]; b1 = in_2[1]; b2 = in_2[2]; b3 = in_2[3]; b4 = in_2[4];
  //   b5 = in_2[5]; b6 = in_2[6]; b7 = in_2[7]; m0[14:8] = {7{m0[15]}}; m1[14:9] = {6{m1[15]}};
  //   m2 (some bits) = {{5{m2[15]}}, m2[1]}; m3 (some bits) = {{4{m3[15]}}, {2{m3[2]}}};
  //   m4 (some bits) = {{3{m4[15]}}, {3{m4[3]}}}; m5 (some bits) = {{2{m5[15]}}, {4{m5[4]}}};
  //   m6 (some bits) = {m6[15], {5{m6[5]}}}; m7[5:0] = {6{m7[6]}}

  // Notes on the sheet:
  //   Cout
endmodule
