// Logisim project Oprs_logicas.circ as structural Verilog
module AND (
  input  [7:0] in_1,
  input  [7:0] in_2,
  output [7:0] out_3
);

  and and_1 (out_3[7], in_1[7], in_2[7]);
  and and_2 (out_3[6], in_1[6], in_2[6]);
  and and_3 (out_3[5], in_1[5], in_2[5]);
  and and_4 (out_3[4], in_1[4], in_2[4]);
  and and_5 (out_3[3], in_1[3], in_2[3]);
  and and_6 (out_3[2], in_1[2], in_2[2]);
  and and_7 (out_3[1], in_1[1], in_2[1]);
  and and_8 (out_3[0], in_1[0], in_2[0]);

  // Other names for the same wires on the sheet: a0 = in_1[0]; a1 = in_1[1]; a2 = in_1[2]; a3 = in_1[3]; a4 = in_1[4];
  //   a5 = in_1[5]; a6 = in_1[6]; a7 = in_1[7]; b0 = in_2[0]; b1 = in_2[1]; b2 = in_2[2]; b3 = in_2[3]; b4 = in_2[4];
  //   b5 = in_2[5]; b6 = in_2[6]; b7 = in_2[7]
endmodule

module OR (
  input  [7:0] in_1,
  input  [7:0] in_2,
  output [7:0] out_3
);

  or or_1 (out_3[7], in_1[7], in_2[7]);
  or or_2 (out_3[6], in_1[6], in_2[6]);
  or or_3 (out_3[5], in_1[5], in_2[5]);
  or or_4 (out_3[4], in_1[4], in_2[4]);
  or or_5 (out_3[3], in_1[3], in_2[3]);
  or or_6 (out_3[2], in_1[2], in_2[2]);
  or or_7 (out_3[0], in_1[0], in_2[0]);
  or or_8 (out_3[1], in_1[1], in_2[1]);

  // Other names for the same wires on the sheet: a0 = in_1[0]; a1 = in_1[1]; a2 = in_1[2]; a3 = in_1[3]; a4 = in_1[4];
  //   a5 = in_1[5]; a6 = in_1[6]; a7 = in_1[7]; b0 = in_2[0]; b1 = in_2[1]; b2 = in_2[2]; b3 = in_2[3]; b4 = in_2[4];
  //   b5 = in_2[5]; b6 = in_2[6]; b7 = in_2[7]
endmodule

module XOR (
  input  [7:0] in_1,
  input  [7:0] in_2,
  output [7:0] out_3
);

  xor xor_1 (out_3[7], in_1[7], in_2[7]);
  xor xor_2 (out_3[6], in_1[6], in_2[6]);
  xor xor_3 (out_3[5], in_1[5], in_2[5]);
  xor xor_4 (out_3[4], in_1[4], in_2[4]);
  xor xor_5 (out_3[3], in_1[3], in_2[3]);
  xor xor_6 (out_3[2], in_1[2], in_2[2]);
  xor xor_7 (out_3[1], in_1[1], in_2[1]);
  xor xor_8 (out_3[0], in_1[0], in_2[0]);

  // Other names for the same wires on the sheet: a0 = in_1[0]; a1 = in_1[1]; a2 = in_1[2]; a3 = in_1[3]; a4 = in_1[4];
  //   a5 = in_1[5]; a6 = in_1[6]; a7 = in_1[7]; b0 = in_2[0]; b1 = in_2[1]; b2 = in_2[2]; b3 = in_2[3]; b4 = in_2[4];
  //   b5 = in_2[5]; b6 = in_2[6]; b7 = in_2[7]
endmodule

module NOT (
  input  [7:0] in_1,
  output [7:0] out_2
);

  not not_1 (out_2[7], in_1[7]);
  not not_2 (out_2[5], in_1[5]);
  not not_3 (out_2[6], in_1[6]);
  not not_4 (out_2[4], in_1[4]);
  not not_5 (out_2[3], in_1[3]);
  not not_6 (out_2[0], in_1[0]);
  not not_7 (out_2[1], in_1[1]);
  not not_8 (out_2[2], in_1[2]);
endmodule
