// Logisim project Seletor_de_8bits.circ as structural Verilog: 3 circuits, main circuit main
module main (
  input  [3:0] in_1,
  input  [7:0] in_2,
  output [7:0] out_3
);

  wire [7:0] array_demux_8bits_1_out_3, array_demux_8bits_1_out_4, array_demux_8bits_1_out_5,
       array_demux_8bits_1_out_6, array_demux_8bits_1_out_7, array_demux_8bits_1_out_8,
       array_demux_8bits_1_out_9, array_demux_8bits_1_out_10, array_demux_8bits_1_out_11,
       array_demux_8bits_1_out_12, array_demux_8bits_1_out_13;

  Array_DEMUX_8bits array_demux_8bits_1 (
    .in_1(in_2), .in_2(in_1), .out_3(array_demux_8bits_1_out_3), .out_4(array_demux_8bits_1_out_4),
    .out_5(array_demux_8bits_1_out_5), .out_6(array_demux_8bits_1_out_6), .out_7(array_demux_8bits_1_out_7),
    .out_8(array_demux_8bits_1_out_8), .out_9(array_demux_8bits_1_out_9),
    .out_10(array_demux_8bits_1_out_10), .out_11(array_demux_8bits_1_out_11),
    .out_12(array_demux_8bits_1_out_12), .out_13(array_demux_8bits_1_out_13));
  // Probe on array_demux_8bits_1_out_7
  // Probe on array_demux_8bits_1_out_3
  Array_MUX_8bits array_mux_8bits_1 (
    .in_1(array_demux_8bits_1_out_7), .in_2(array_demux_8bits_1_out_4), .in_3(array_demux_8bits_1_out_5),
    .in_4(array_demux_8bits_1_out_6), .in_5(array_demux_8bits_1_out_3), .in_6(array_demux_8bits_1_out_8),
    .in_7(array_demux_8bits_1_out_9), .in_8(array_demux_8bits_1_out_10), .in_9(array_demux_8bits_1_out_11),
    .in_10(array_demux_8bits_1_out_12), .in_11(array_demux_8bits_1_out_13), .in_12(in_1), .out_13(out_3));

  // Notes on the sheet:
  //   Como também para a saída adequada 
  //   O seletor de 8 bits serve para direcionar os 8 bits para uma função
endmodule

module Array_MUX_8bits (
  input  [7:0] in_1,
  input  [7:0] in_2,
  input  [7:0] in_3,
  input  [7:0] in_4,
  input  [7:0] in_5,
  input  [7:0] in_6,
  input  [7:0] in_7,
  input  [7:0] in_8,
  input  [7:0] in_9,
  input  [7:0] in_10,
  input  [7:0] in_11,
  input  [3:0] in_12,
  output [7:0] out_13
);

  wire pull_resistor_1_node;

  Pull_Resistor pull_resistor_1 (.node(pull_resistor_1_node));
  Multiplexer #(.select(4), .enable("false")) multiplexer_1 (
    .in0(pull_resistor_1_node), .in1(in_2[7]), .in2(in_6[7]), .in3(in_9[7]), .in4(in_3[7]), .in5(in_7[7]),
    .in6(in_10[7]), .in7(in_4[7]), .in8(in_8[7]), .in9(in_11[7]), .in10(in_1[7]), .in11(in_5[7]),
    .in12(pull_resistor_1_node), .in13(pull_resistor_1_node), .in14(pull_resistor_1_node),
    .in15(pull_resistor_1_node), .out(out_13[7]), .sel(in_12));
  Multiplexer #(.select(4), .enable("false")) multiplexer_2 (
    .in0(pull_resistor_1_node), .in1(in_2[6]), .in2(in_6[6]), .in3(in_9[6]), .in4(in_3[6]), .in5(in_7[6]),
    .in6(in_10[6]), .in7(in_4[6]), .in8(in_8[6]), .in9(in_11[6]), .in10(in_1[6]), .in11(in_5[6]),
    .in12(pull_resistor_1_node), .in13(pull_resistor_1_node), .in14(pull_resistor_1_node),
    .in15(pull_resistor_1_node), .out(out_13[6]), .sel(in_12));
  Multiplexer #(.select(4), .enable("false")) multiplexer_3 (
    .in0(pull_resistor_1_node), .in1(in_2[5]), .in2(in_6[5]), .in3(in_9[5]), .in4(in_3[5]), .in5(in_7[5]),
    .in6(in_10[5]), .in7(in_4[5]), .in8(in_8[5]), .in9(in_11[5]), .in10(in_1[5]), .in11(in_5[5]),
    .in12(pull_resistor_1_node), .in13(pull_resistor_1_node), .in14(pull_resistor_1_node),
    .in15(pull_resistor_1_node), .out(out_13[5]), .sel(in_12));
  Multiplexer #(.select(4), .enable("false")) multiplexer_4 (
    .in0(pull_resistor_1_node), .in1(in_2[4]), .in2(in_6[4]), .in3(in_9[4]), .in4(in_3[4]), .in5(in_7[4]),
    .in6(in_10[4]), .in7(in_4[4]), .in8(in_8[4]), .in9(in_11[4]), .in10(in_1[4]), .in11(in_5[4]),
    .in12(pull_resistor_1_node), .in13(pull_resistor_1_node), .in14(pull_resistor_1_node),
    .in15(pull_resistor_1_node), .out(out_13[4]), .sel(in_12));
  Multiplexer #(.select(4), .enable("false")) multiplexer_5 (
    .in0(pull_resistor_1_node), .in1(in_2[3]), .in2(in_6[3]), .in3(in_9[3]), .in4(in_3[3]), .in5(in_7[3]),
    .in6(in_10[3]), .in7(in_4[3]), .in8(in_8[3]), .in9(in_11[3]), .in10(in_1[3]), .in11(in_5[3]),
    .in12(pull_resistor_1_node), .in13(pull_resistor_1_node), .in14(pull_resistor_1_node),
    .in15(pull_resistor_1_node), .out(out_13[3]), .sel(in_12));
  Multiplexer #(.select(4), .enable("false")) multiplexer_6 (
    .in0(pull_resistor_1_node), .in1(in_2[2]), .in2(in_6[2]), .in3(in_9[2]), .in4(in_3[2]), .in5(in_7[2]),
    .in6(in_10[2]), .in7(in_4[2]), .in8(in_8[2]), .in9(in_11[2]), .in10(in_1[2]), .in11(in_5[2]),
    .in12(pull_resistor_1_node), .in13(pull_resistor_1_node), .in14(pull_resistor_1_node),
    .in15(pull_resistor_1_node), .out(out_13[2]), .sel(in_12));
  Multiplexer #(.select(4), .enable("false")) multiplexer_7 (
    .in0(pull_resistor_1_node), .in1(in_2[1]), .in2(in_6[1]), .in3(in_9[1]), .in4(in_3[1]), .in5(in_7[1]),
    .in6(in_10[1]), .in7(in_4[1]), .in8(in_8[1]), .in9(in_11[1]), .in10(in_1[1]), .in11(in_5[1]),
    .in12(pull_resistor_1_node), .in13(pull_resistor_1_node), .in14(pull_resistor_1_node),
    .in15(pull_resistor_1_node), .out(out_13[1]), .sel(in_12));
  Multiplexer #(.select(4), .enable("false")) multiplexer_8 (
    .in0(pull_resistor_1_node), .in1(in_2[0]), .in2(in_6[0]), .in3(in_9[0]), .in4(in_3[0]), .in5(in_7[0]),
    .in6(in_10[0]), .in7(in_4[0]), .in8(in_8[0]), .in9(in_11[0]), .in10(in_1[0]), .in11(in_5[0]),
    .in12(pull_resistor_1_node), .in13(pull_resistor_1_node), .in14(pull_resistor_1_node),
    .in15(pull_resistor_1_node), .out(out_13[0]), .sel(in_12));

  // Other names for the same wires on the sheet: _010 = in_1[0]; _110 = in_1[1]; _210 = in_1[2]; _310 = in_1[3];
  //   _410 = in_1[4]; _510 = in_1[5]; _610 = in_1[6]; _710 = in_1[7]; _01 = in_2[0]; _11 = in_2[1]; _21 = in_2[2];
  //   _31 = in_2[3]; _41 = in_2[4]; _51 = in_2[5]; _61 = in_2[6]; _71 = in_2[7]; _04 = in_3[0]; _14 = in_3[1];
  //   _24 = in_3[2]; _34 = in_3[3]; _44 = in_3[4]; _54 = in_3[5]; _64 = in_3[6]; _74 = in_3[7]; _07 = in_4[0];
  //   _17 = in_4[1]; _27 = in_4[2]; _37 = in_4[3]; _47 = in_4[4]; _57 = in_4[5]; _67 = in_4[6]; _77 = in_4[7];
  //   _011 = in_5[0]; _111 = in_5[1]; _211 = in_5[2]; _311 = in_5[3]; _411 = in_5[4]; _511 = in_5[5]; _611 = in_5[6];
  //   _711 = in_5[7]; _02 = in_6[0]; _12 = in_6[1]; _22 = in_6[2]; _32 = in_6[3]; _42 = in_6[4]; _52 = in_6[5];
  //   _62 = in_6[6]; _72 = in_6[7]; _05 = in_7[0]; _15 = in_7[1]; _25 = in_7[2]; _35 = in_7[3]; _45 = in_7[4];
  //   _55 = in_7[5]; _65 = in_7[6]; _75 = in_7[7]; _08 = in_8[0]; _18 = in_8[1]; _28 = in_8[2]; _38 = in_8[3];
  //   _48 = in_8[4]; _58 = in_8[5]; _68 = in_8[6]; _78 = in_8[7]; _03 = in_9[0]; _13 = in_9[1]; _23 = in_9[2];
  //   _33 = in_9[3]; _43 = in_9[4]; _53 = in_9[5]; _63 = in_9[6]; _73 = in_9[7]; _06 = in_10[0]; _16 = in_10[1];
  //   _26 = in_10[2]; _36 = in_10[3]; _46 = in_10[4]; _56 = in_10[5]; _66 = in_10[6]; _76 = in_10[7]; _09 = in_11[0];
  //   _19 = in_11[1]; _29 = in_11[2]; _39 = in_11[3]; _49 = in_11[4]; _59 = in_11[5]; _69 = in_11[6]; _79 = in_11[7];
  //   A0 = out_13[0]; A1 = out_13[1]; A2 = out_13[2]; A3 = out_13[3]; A4 = out_13[4]; A5 = out_13[5]; A6 = out_13[6];
  //   A7 = out_13[7]

  // Notes on the sheet:
  //   ENTRADA
  //   SAÍDAS PARA AS FUNÇÕES
endmodule

module Array_DEMUX_8bits (
  input  [7:0] in_1,
  input  [3:0] in_2,
  output [7:0] out_3,
  output [7:0] out_4,
  output [7:0] out_5,
  output [7:0] out_6,
  output [7:0] out_7,
  output [7:0] out_8,
  output [7:0] out_9,
  output [7:0] out_10,
  output [7:0] out_11,
  output [7:0] out_12,
  output [7:0] out_13
);

  Demultiplexer #(.select(4), .enable("false")) demultiplexer_1 (
    .out1(out_4[7]), .out2(out_8[7]), .out3(out_11[7]), .out4(out_5[7]), .out5(out_9[7]), .out6(out_12[7]),
    .out7(out_6[7]), .out8(out_10[7]), .out9(out_13[7]), .out10(out_3[7]), .out11(out_7[7]), .in(in_1[7]),
    .sel(in_2));  // open: out0, out12, out13, out14, out15
  Demultiplexer #(.select(4), .enable("false")) demultiplexer_2 (
    .out1(out_4[6]), .out2(out_8[6]), .out3(out_11[6]), .out4(out_5[6]), .out5(out_9[6]), .out6(out_12[6]),
    .out7(out_6[6]), .out8(out_10[6]), .out9(out_13[6]), .out10(out_3[6]), .out11(out_7[6]), .in(in_1[6]),
    .sel(in_2));  // open: out0, out12, out13, out14, out15
  Demultiplexer #(.select(4), .enable("false")) demultiplexer_3 (
    .out1(out_4[5]), .out2(out_8[5]), .out3(out_11[5]), .out4(out_5[5]), .out5(out_9[5]), .out6(out_12[5]),
    .out7(out_6[5]), .out8(out_10[5]), .out9(out_13[5]), .out10(out_3[5]), .out11(out_7[5]), .in(in_1[5]),
    .sel(in_2));  // open: out0, out12, out13, out14, out15
  Demultiplexer #(.select(4), .enable("false")) demultiplexer_4 (
    .out1(out_4[4]), .out2(out_8[4]), .out3(out_11[4]), .out4(out_5[4]), .out5(out_9[4]), .out6(out_12[4]),
    .out7(out_6[4]), .out8(out_10[4]), .out9(out_13[4]), .out10(out_3[4]), .out11(out_7[4]), .in(in_1[4]),
    .sel(in_2));  // open: out0, out12, out13, out14, out15
  Demultiplexer #(.select(4), .enable("false")) demultiplexer_5 (
    .out1(out_4[3]), .out2(out_8[3]), .out3(out_11[3]), .out4(out_5[3]), .out5(out_9[3]), .out6(out_12[3]),
    .out7(out_6[3]), .out8(out_10[3]), .out9(out_13[3]), .out10(out_3[3]), .out11(out_7[3]), .in(in_1[3]),
    .sel(in_2));  // open: out0, out12, out13, out14, out15
  Demultiplexer #(.select(4), .enable("false")) demultiplexer_6 (
    .out1(out_4[2]), .out2(out_8[2]), .out3(out_11[2]), .out4(out_5[2]), .out5(out_9[2]), .out6(out_12[2]),
    .out7(out_6[2]), .out8(out_10[2]), .out9(out_13[2]), .out10(out_3[2]), .out11(out_7[2]), .in(in_1[2]),
    .sel(in_2));  // open: out0, out12, out13, out14, out15
  Demultiplexer #(.select(4), .enable("false")) demultiplexer_7 (
    .out1(out_4[1]), .out2(out_8[1]), .out3(out_11[1]), .out4(out_5[1]), .out5(out_9[1]), .out6(out_12[1]),
    .out7(out_6[1]), .out8(out_10[1]), .out9(out_13[1]), .out10(out_3[1]), .out11(out_7[1]), .in(in_1[1]),
    .sel(in_2));  // open: out0, out12, out13, out14, out15
  Demultiplexer #(.select(4), .enable("false")) demultiplexer_8 (
    .out1(out_4[0]), .out2(out_8[0]), .out3(out_11[0]), .out4(out_5[0]), .out5(out_9[0]), .out6(out_12[0]),
    .out7(out_6[0]), .out8(out_10[0]), .out9(out_13[0]), .out10(out_3[0]), .out11(out_7[0]), .in(in_1[0]),
    .sel(in_2));  // open: out0, out12, out13, out14, out15

  // Other names for the same wires on the sheet: A0 = in_1[0]; A1 = in_1[1]; A2 = in_1[2]; A3 = in_1[3]; A4 = in_1[4];
  //   A5 = in_1[5]; A6 = in_1[6]; A7 = in_1[7]; _010 = out_3[0]; _110 = out_3[1]; _210 = out_3[2]; _310 = out_3[3];
  //   _410 = out_3[4]; _510 = out_3[5]; _610 = out_3[6]; _710 = out_3[7]; _01 = out_4[0]; _11 = out_4[1];
  //   _21 = out_4[2]; _31 = out_4[3]; _41 = out_4[4]; _51 = out_4[5]; _61 = out_4[6]; _71 = out_4[7]; _04 = out_5[0];
  //   _14 = out_5[1]; _24 = out_5[2]; _34 = out_5[3]; _44 = out_5[4]; _54 = out_5[5]; _64 = out_5[6]; _74 = out_5[7];
  //   _07 = out_6[0]; _17 = out_6[1]; _27 = out_6[2]; _37 = out_6[3]; _47 = out_6[4]; _57 = out_6[5]; _67 = out_6[6];
  //   _77 = out_6[7]; _011 = out_7[0]; _111 = out_7[1]; _211 = out_7[2]; _311 = out_7[3]; _411 = out_7[4];
  //   _511 = out_7[5]; _611 = out_7[6]; _711 = out_7[7]; _02 = out_8[0]; _12 = out_8[1]; _22 = out_8[2];
  //   _32 = out_8[3]; _42 = out_8[4]; _52 = out_8[5]; _62 = out_8[6]; _72 = out_8[7]; _05 = out_9[0]; _15 = out_9[1];
  //   _25 = out_9[2]; _35 = out_9[3]; _45 = out_9[4]; _55 = out_9[5]; _65 = out_9[6]; _75 = out_9[7]; _08 = out_10[0];
  //   _18 = out_10[1]; _28 = out_10[2]; _38 = out_10[3]; _48 = out_10[4]; _58 = out_10[5]; _68 = out_10[6];
  //   _78 = out_10[7]; _03 = out_11[0]; _13 = out_11[1]; _23 = out_11[2]; _33 = out_11[3]; _43 = out_11[4];
  //   _53 = out_11[5]; _63 = out_11[6]; _73 = out_11[7]; _06 = out_12[0]; _16 = out_12[1]; _26 = out_12[2];
  //   _36 = out_12[3]; _46 = out_12[4]; _56 = out_12[5]; _66 = out_12[6]; _76 = out_12[7]; _09 = out_13[0];
  //   _19 = out_13[1]; _29 = out_13[2]; _39 = out_13[3]; _49 = out_13[4]; _59 = out_13[5]; _69 = out_13[6];
  //   _79 = out_13[7]

  // Notes on the sheet:
  //   ENTRADA
  //   SELEÇÃO DE FUNÇÃO
  //   SAÍDAS PARA AS FUNÇÕES
endmodule
