// Logisim project Somador_Subtrator.circ as structural Verilog
module Somador_completo (
  input  A,
  input  B,
  input  cin,
  output co,
  output s
);

  wire and_1_out, and_2_out, and_3_out, xor_1_out;

  and and_1 (and_1_out, A, B);
  and and_2 (and_2_out, A, cin);
  and and_3 (and_3_out, B, cin);
  xor xor_1 (xor_1_out, A, B);
  xor xor_2 (s, xor_1_out, cin);
  or or_1 (co, and_1_out, and_2_out, and_3_out);
endmodule

module Subtrator_completo (
  input  A,
  input  B,
  input  Te,
  output To,
  output s
);

  wire and_1_out, and_2_out, and_3_out, xor_1_out;

  and and_1 (and_1_out, ~A, B);  // AND_Gate
  and and_2 (and_2_out, ~A, Te);  // AND_Gate
  and and_3 (and_3_out, B, Te);
  xor xor_1 (xor_1_out, A, B);
  xor xor_2 (s, xor_1_out, Te);
  or or_1 (To, and_1_out, and_2_out, and_3_out);
endmodule

module Meio_somador (
  input  A,
  input  B,
  output Co,
  output S
);

  and and_1 (Co, A, B);
  xor xor_1 (S, A, B);
endmodule

module Meio_subtrator (
  input  A,
  input  B,
  output To,
  output S
);

  and and_1 (To, ~A, B);  // AND_Gate
  xor xor_1 (S, A, B);
endmodule

module ADD16 (
  input  [15:0] in_1,
  input  in_2,
  input  [15:0] in_3,
  output [15:0] out_4,
  output out_5
);

  wire somador_completo_1_co, somador_completo_2_co, somador_completo_3_co, somador_completo_4_co,
       somador_completo_5_co, somador_completo_6_co, somador_completo_7_co, somador_completo_8_co,
       somador_completo_9_co, somador_completo_10_co, somador_completo_11_co, somador_completo_12_co,
       somador_completo_13_co, somador_completo_14_co, somador_completo_15_co;

  Somador_completo somador_completo_1 (.A(in_1[0]), .B(in_3[0]), .cin(in_2), .co(somador_completo_1_co), .s(out_4[0]));
  Somador_completo somador_completo_2 (
    .A(in_1[1]), .B(in_3[1]), .cin(somador_completo_1_co), .co(somador_completo_2_co), .s(out_4[1]));
  Somador_completo somador_completo_3 (
    .A(in_1[2]), .B(in_3[2]), .cin(somador_completo_2_co), .co(somador_completo_3_co), .s(out_4[2]));
  Somador_completo somador_completo_4 (
    .A(in_1[3]), .B(in_3[3]), .cin(somador_completo_3_co), .co(somador_completo_4_co), .s(out_4[3]));
  Somador_completo somador_completo_5 (
    .A(in_1[4]), .B(in_3[4]), .cin(somador_completo_4_co), .co(somador_completo_5_co), .s(out_4[4]));
  Somador_completo somador_completo_6 (
    .A(in_1[5]), .B(in_3[5]), .cin(somador_completo_5_co), .co(somador_completo_6_co), .s(out_4[5]));
  Somador_completo somador_completo_7 (
    .A(in_1[6]), .B(in_3[6]), .cin(somador_completo_6_co), .co(somador_completo_7_co), .s(out_4[6]));
  Somador_completo somador_completo_8 (
    .A(in_1[7]), .B(in_3[7]), .cin(somador_completo_7_co), .co(somador_completo_8_co), .s(out_4[7]));
  Somador_completo somador_completo_9 (
    .A(in_1[8]), .B(in_3[8]), .cin(somador_completo_8_co), .co(somador_completo_9_co), .s(out_4[8]));
  Somador_completo somador_completo_10 (
    .A(in_1[9]), .B(in_3[9]), .cin(somador_completo_9_co), .co(somador_completo_10_co), .s(out_4[9]));
  Somador_completo somador_completo_11 (
    .A(in_1[10]), .B(in_3[10]), .cin(somador_completo_10_co), .co(somador_completo_11_co), .s(out_4[10]));
  Somador_completo somador_completo_12 (
    .A(in_1[11]), .B(in_3[11]), .cin(somador_completo_11_co), .co(somador_completo_12_co), .s(out_4[11]));
  Somador_completo somador_completo_13 (
    .A(in_1[12]), .B(in_3[12]), .cin(somador_completo_12_co), .co(somador_completo_13_co), .s(out_4[12]));
  Somador_completo somador_completo_14 (
    .A(in_1[13]), .B(in_3[13]), .cin(somador_completo_13_co), .co(somador_completo_14_co), .s(out_4[13]));
  Somador_completo somador_completo_15 (
    .A(in_1[14]), .B(in_3[14]), .cin(somador_completo_14_co), .co(somador_completo_15_co), .s(out_4[14]));
  Somador_completo somador_completo_16 (
    .A(in_1[15]), .B(in_3[15]), .cin(somador_completo_15_co), .co(out_5), .s(out_4[15]));

  // Other names for the same wires on the sheet: a0 = in_1[0]; a1 = in_1[1]; a2 = in_1[2]; a3 = in_1[3]; a4 = in_1[4];
  //   a5 = in_1[5]; a6 = in_1[6]; a7 = in_1[7]; a8 = in_1[8]; a9 = in_1[9]; a10 = in_1[10]; a11 = in_1[11];
  //   a12 = in_1[12]; a13 = in_1[13]; a14 = in_1[14]; a15 = in_1[15]; b0 = in_3[0]; b1 = in_3[1]; b2 = in_3[2];
  //   b3 = in_3[3]; b4 = in_3[4]; b5 = in_3[5]; b6 = in_3[6]; b7 = in_3[7]; b8 = in_3[8]; b9 = in_3[9];
  //   b10 = in_3[10]; b11 = in_3[11]; b12 = in_3[12]; b13 = in_3[13]; b14 = in_3[14]; b15 = in_3[15]; s0 = out_4[0];
  //   s1 = out_4[1]; s2 = out_4[2]; s3 = out_4[3]; s4 = out_4[4]; s5 = out_4[5]; s6 = out_4[6]; s7 = out_4[7];
  //   s8 = out_4[8]; s9 = out_4[9]; s10 = out_4[10]; s11 = out_4[11]; s12 = out_4[12]; s13 = out_4[13];
  //   s14 = out_4[14]; s15 = out_4[15]

  // Notes on the sheet:
  //   Cin
endmodule

module ADD8 (
  input  [7:0] in_1,
  input  in_2,
  input  [7:0] in_3,
  output [7:0] out_4,
  output out_5
);

  wire somador_completo_1_co, somador_completo_2_co, somador_completo_3_co, somador_completo_4_co,
       somador_completo_5_co, somador_completo_6_co, somador_completo_7_co;

  Somador_completo somador_completo_1 (.A(in_1[0]), .B(in_3[0]), .cin(in_2), .co(somador_completo_1_co), .s(out_4[0]));
  Somador_completo somador_completo_2 (
    .A(in_1[1]), .B(in_3[1]), .cin(somador_completo_1_co), .co(somador_completo_2_co), .s(out_4[1]));
  Somador_completo somador_completo_3 (
    .A(in_1[2]), .B(in_3[2]), .cin(somador_completo_2_co), .co(somador_completo_3_co), .s(out_4[2]));
  Somador_completo somador_completo_4 (
    .A(in_1[3]), .B(in_3[3]), .cin(somador_completo_3_co), .co(somador_completo_4_co), .s(out_4[3]));
  Somador_completo somador_completo_5 (
    .A(in_1[4]), .B(in_3[4]), .cin(somador_completo_4_co), .co(somador_completo_5_co), .s(out_4[4]));
  Somador_completo somador_completo_6 (
    .A(in_1[5]), .B(in_3[5]), .cin(somador_completo_5_co), .co(somador_completo_6_co), .s(out_4[5]));
  Somador_completo somador_completo_7 (
    .A(in_1[6]), .B(in_3[6]), .cin(somador_completo_6_co), .co(somador_completo_7_co), .s(out_4[6]));
  Somador_completo somador_completo_8 (.A(in_1[7]), .B(in_3[7]), .cin(somador_completo_7_co), .co(out_5), .s(out_4[7]));

  // Other names for the same wires on the sheet: a0 = in_1[0]; a1 = in_1[1]; a2 = in_1[2]; a3 = in_1[3]; a4 = in_1[4];
  //   a5 = in_1[5]; a6 = in_1[6]; a7 = in_1[7]; b0 = in_3[0]; b1 = in_3[1]; b2 = in_3[2]; b3 = in_3[3]; b4 = in_3[4];
  //   b5 = in_3[5]; b6 = in_3[6]; b7 = in_3[7]; s0 = out_4[0]; s1 = out_4[1]; s2 = out_4[2]; s3 = out_4[3];
  //   s4 = out_4[4]; s5 = out_4[5]; s6 = out_4[6]; s7 = out_4[7]

  // Notes on the sheet:
  //   Cin
endmodule

module SUB8 (
  input  Ti,
  input  [7:0] in_2,
  input  [7:0] in_3,
  output [7:0] out_4,
  output Tout
);

  wire subtrator_completo_1_to, subtrator_completo_2_to, subtrator_completo_3_to, subtrator_completo_4_to,
       subtrator_completo_5_to, subtrator_completo_6_to, subtrator_completo_7_to;

  Subtrator_completo subtrator_completo_1 (
    .A(in_2[0]), .B(in_3[0]), .Te(Ti), .To(subtrator_completo_1_to), .s(out_4[0]));
  Subtrator_completo subtrator_completo_2 (
    .A(in_2[1]), .B(in_3[1]), .Te(subtrator_completo_1_to), .To(subtrator_completo_2_to), .s(out_4[1]));
  Subtrator_completo subtrator_completo_3 (
    .A(in_2[2]), .B(in_3[2]), .Te(subtrator_completo_2_to), .To(subtrator_completo_3_to), .s(out_4[2]));
  Subtrator_completo subtrator_completo_4 (
    .A(in_2[3]), .B(in_3[3]), .Te(subtrator_completo_3_to), .To(subtrator_completo_4_to), .s(out_4[3]));
  Subtrator_completo subtrator_completo_5 (
    .A(in_2[4]), .B(in_3[4]), .Te(subtrator_completo_4_to), .To(subtrator_completo_5_to), .s(out_4[4]));
  Subtrator_completo subtrator_completo_6 (
    .A(in_2[5]), .B(in_3[5]), .Te(subtrator_completo_5_to), .To(subtrator_completo_6_to), .s(out_4[5]));
  Subtrator_completo subtrator_completo_7 (
    .A(in_2[6]), .B(in_3[6]), .Te(subtrator_completo_6_to), .To(subtrator_completo_7_to), .s(out_4[6]));
  Subtrator_completo subtrator_completo_8 (
    .A(in_2[7]), .B(in_3[7]), .Te(subtrator_completo_7_to), .To(Tout), .s(out_4[7]));

  // Other names for the same wires on the sheet: a0 = in_2[0]; a1 = in_2[1]; a2 = in_2[2]; a3 = in_2[3]; a4 = in_2[4];
  //   a5 = in_2[5]; a6 = in_2[6]; a7 = in_2[7]; b0 = in_3[0]; b1 = in_3[1]; b2 = in_3[2]; b3 = in_3[3]; b4 = in_3[4];
  //   b5 = in_3[5]; b6 = in_3[6]; b7 = in_3[7]; s0 = out_4[0]; s1 = out_4[1]; s2 = out_4[2]; s3 = out_4[3];
  //   s4 = out_4[4]; s5 = out_4[5]; s6 = out_4[6]; s7 = out_4[7]
endmodule
