// Logisim project ULA.circ as structural Verilog: 1 circuit, main circuit main
module main (
  input  [3:0] in_1,
  input  in_2,
  input  [7:0] in_3,
  input  [7:0] in_4,
  input  in_5,
  output [7:0] out_6
);

  wire [7:0] add8_1_out_4, and_1_out_3, multiplicador_8bits_1_out_4, not_1_out_2, or_1_out_3, shifte_1_out_5,
       shifter_1_out_6, sub8_1_out_4, xor_1_out_3;

  ADD8 add8_1 (.in_1(in_3), .in_2(in_2), .in_3(in_4), .out_4(add8_1_out_4));  // open: out_5
  SUB8 sub8_1 (.Ti(in_2), .in_2(in_3), .in_3(in_4), .out_4(sub8_1_out_4));  // open: Tout
  Multiplicador_8bits multiplicador_8bits_1 (
    .in_1(in_3), .in_2(in_4), .out_4(multiplicador_8bits_1_out_4));  // open: out_3
  AND and_1 (.in_1(in_3), .in_2(in_4), .out_3(and_1_out_3));
  OR or_1 (.in_1(in_3), .in_2(in_4), .out_3(or_1_out_3));
  XOR xor_1 (.in_1(in_3), .in_2(in_4), .out_3(xor_1_out_3));
  NOT not_1 (.in_1(in_3), .out_2(not_1_out_2));
  Shifter shifter_1 (.E(in_5), .out_6(shifter_1_out_6), .in_1(in_3), .in_3(in_4[2:0]));  // open: Z, c
  Shifte shifte_1 (.E(in_5), .in_1(in_3), .out_5(shifte_1_out_5), .in_3(in_4[2:0]));  // open: Z
  // Probe on nothing
  Multiplexer #(.select(4), .width(8), .enable("false")) multiplexer_1 (
    .in1(add8_1_out_4), .in2(sub8_1_out_4), .in3(add8_1_out_4), .in4(sub8_1_out_4),
    .in5(multiplicador_8bits_1_out_4), .in6(and_1_out_3), .in7(or_1_out_3), .in8(xor_1_out_3),
    .in9(not_1_out_2), .in10(shifter_1_out_6), .in11(shifte_1_out_5), .out(out_6), .sel(in_1));  // open: in0, in12, in13, in14, in15
endmodule
