// Logisim project Comparador_8bita.circ as structural Verilog: 1 circuit, main circuit main
module main (
  input  A0,
  input  B0,
  input  A1,
  input  B1,
  input  A2,
  input  B2,
  input  A3,
  input  B3,
  input  A4,
  input  B4,
  input  A5,
  input  B5,
  input  A6,
  input  B6,
  input  A7,
  input  B7,
  output out_17,
  output A___B,
  output A___B_2
);

  wire a0_b0, a1_b1, a2_b2, a3_b3, a4_b4, a5_b5, a6_b6, a7_b7, and_1_out, and_2_out, and_3_out, and_4_out,
       and_5_out, and_6_out, and_8_out, and_10_out, and_12_out, and_13_out, lsb_a_b, lsb_a_b_t, lsb_a_b_t_t,
       msb_a_b, msb_a_b_t, msb_a_b_t_t;

  xnor xnor_1 (a0_b0, A0, B0);
  xnor xnor_2 (a1_b1, A1, B1);
  xnor xnor_3 (a2_b2, A2, B2);
  xnor xnor_4 (a4_b4, A4, B4);
  xnor xnor_5 (a3_b3, A3, B3);
  xnor xnor_6 (a5_b5, A5, B5);
  xnor xnor_7 (a6_b6, A6, B6);
  xnor xnor_8 (a7_b7, A7, B7);
  and and_1 (and_1_out, a7_b7, A6, ~B6);  // AND_Gate
  and and_2 (and_2_out, A7, ~B7);  // AND_Gate
  and and_3 (and_3_out, a2_b2, a3_b3, A1, ~B1);  // AND_Gate
  and and_4 (and_4_out, a3_b3, A2, ~B2);  // AND_Gate
  and and_5 (and_5_out, A3, ~B3);  // AND_Gate
  and and_6 (and_6_out, a6_b6, a7_b7, A5, ~B5);  // AND_Gate
  and and_7 (lsb_a_b_t, a0_b0, a1_b1, a2_b2, a3_b3);
  and and_8 (and_8_out, A0, ~B0, a1_b1, a2_b2, a3_b3);  // AND_Gate
  and and_9 (msb_a_b_t, a4_b4, a5_b5, a6_b6, a7_b7);
  and and_10 (and_10_out, A4, ~B4, a5_b5, a6_b6, a7_b7);  // AND_Gate
  or or_1 (lsb_a_b_t_t, and_8_out, and_3_out, and_4_out, and_5_out);
  or or_2 (msb_a_b_t_t, and_10_out, and_6_out, and_1_out, and_2_out);
  nor nor_1 (msb_a_b, msb_a_b_t, msb_a_b_t_t);
  nor nor_2 (lsb_a_b, lsb_a_b_t, lsb_a_b_t_t);
  and and_11 (out_17, lsb_a_b_t, msb_a_b_t);
  and and_12 (and_12_out, lsb_a_b, msb_a_b_t);
  and and_13 (and_13_out, lsb_a_b_t_t, msb_a_b_t);
  or or_3 (A___B, and_12_out, msb_a_b);
  or or_4 (A___B_2, and_13_out, msb_a_b_t_t);

  // Notes on the sheet:
  //   A = B
  //   A = B
  //   A > B
  //   A > B
  //   A < B
  //   A < B
  //   MSB
  //   LSB
  //   A = B
  //   SAÍDAS FINAIS
endmodule
