// Logisim project Double_dabble.circ as structural Verilog
module logica (
  input  A7,
  input  A6,
  input  A5,
  input  A4,
  input  A3,
  input  A2,
  input  A1,
  input  A0,
  output D,
  output C,
  output B,
  output A,
  output D_2,
  output C_2,
  output B_2,
  output A_2
);

  wire shift_add_3_1_lsb, shift_add_3_1_msb, shift_add_3_1_out_6, shift_add_3_1_out_7, shift_add_3_2_lsb,
       shift_add_3_2_msb, shift_add_3_2_out_6, shift_add_3_2_out_7, shift_add_3_3_lsb, shift_add_3_3_msb,
       shift_add_3_3_out_6, shift_add_3_3_out_7, shift_add_3_4_lsb, shift_add_3_4_msb, shift_add_3_4_out_6,
       shift_add_3_4_out_7, shift_add_3_5_lsb, shift_add_3_5_msb, shift_add_3_5_out_6, shift_add_3_5_out_7;

  shift_add_3 shift_add_3_1 (
    .in_1(A5), .in_2(A6), .in_3(A7), .in_4(1'b0), .MSB(shift_add_3_1_msb), .out_6(shift_add_3_1_out_6),
    .out_7(shift_add_3_1_out_7), .LSB(shift_add_3_1_lsb));
  shift_add_3 shift_add_3_2 (
    .in_1(A4), .in_2(shift_add_3_1_lsb), .in_3(shift_add_3_1_out_7), .in_4(shift_add_3_1_out_6),
    .MSB(shift_add_3_2_msb), .out_6(shift_add_3_2_out_6), .out_7(shift_add_3_2_out_7), .LSB(shift_add_3_2_lsb));
  shift_add_3 shift_add_3_3 (
    .in_1(A3), .in_2(shift_add_3_2_lsb), .in_3(shift_add_3_2_out_7), .in_4(shift_add_3_2_out_6),
    .MSB(shift_add_3_3_msb), .out_6(shift_add_3_3_out_6), .out_7(shift_add_3_3_out_7), .LSB(shift_add_3_3_lsb));
  shift_add_3 shift_add_3_4 (
    .in_1(shift_add_3_3_msb), .in_2(shift_add_3_2_msb), .in_3(shift_add_3_1_msb), .in_4(1'b0),
    .MSB(shift_add_3_4_msb), .out_6(shift_add_3_4_out_6), .out_7(shift_add_3_4_out_7), .LSB(shift_add_3_4_lsb));
  shift_add_3 shift_add_3_5 (
    .in_1(A2), .in_2(shift_add_3_3_lsb), .in_3(shift_add_3_3_out_7), .in_4(shift_add_3_3_out_6),
    .MSB(shift_add_3_5_msb), .out_6(shift_add_3_5_out_6), .out_7(shift_add_3_5_out_7), .LSB(shift_add_3_5_lsb));
  shift_add_3 shift_add_3_6 (
    .in_1(shift_add_3_5_msb), .in_2(shift_add_3_4_lsb), .in_3(shift_add_3_4_out_7),
    .in_4(shift_add_3_4_out_6), .MSB(shift_add_3_4_msb), .out_6(D), .out_7(C), .LSB(B));
  shift_add_3 shift_add_3_7 (
    .in_1(A1), .in_2(shift_add_3_5_lsb), .in_3(shift_add_3_5_out_7), .in_4(shift_add_3_5_out_6), .MSB(A),
    .out_6(D_2), .out_7(C_2), .LSB(B_2));

  assign A_2 = A0;
  // also tied to GND on the sheet: shift_add_3_4_msb

  // Notes on the sheet:
  //   DEZENAS
  //   UNIDADES
endmodule

module shift_add_3 (
  input  in_1,
  input  in_2,
  input  in_3,
  input  in_4,
  output MSB,
  output out_6,
  output out_7,
  output LSB
);

  wire and_1_out, and_2_out, and_3_out, and_4_out, and_5_out, and_6_out, and_7_out, and_8_out,
       comparador_de_mag_1_out_11, somador_4bits_1_lsb_3, somador_4bits_1_msb_3, somador_4bits_1_out_11,
       somador_4bits_1_out_12;

  somador_4bits somador_4bits_1 (
    .out_11(somador_4bits_1_out_11), .out_12(somador_4bits_1_out_12), .MSB_3(somador_4bits_1_msb_3),
    .MSB(1'b0), .in_2(1'b0), .LSB(1'b1), .in_4(1'b1), .MSB_2(in_4), .in_6(in_3), .LSB_2(in_2), .in_8(in_1),
    .LSB_3(somador_4bits_1_lsb_3), .in_9(comparador_de_mag_1_out_11));  // open: out_14
  comparador_de_mag comparador_de_mag_1 (
    .A0(in_1), .B0(1'b0), .A1(in_2), .B1(1'b0), .A2(in_3), .B2(1'b1), .A3(in_4), .B3(1'b0),
    .out_11(comparador_de_mag_1_out_11));  // open: out_9, out_10
  and and_1 (and_1_out, somador_4bits_1_msb_3, comparador_de_mag_1_out_11);
  and and_2 (and_2_out, somador_4bits_1_out_12, comparador_de_mag_1_out_11);
  and and_3 (and_3_out, somador_4bits_1_out_11, comparador_de_mag_1_out_11);
  and and_4 (and_4_out, somador_4bits_1_lsb_3, comparador_de_mag_1_out_11);
  and and_5 (and_5_out, in_1, ~comparador_de_mag_1_out_11);  // AND_Gate
  and and_6 (and_6_out, in_2, ~comparador_de_mag_1_out_11);  // AND_Gate
  and and_7 (and_7_out, in_3, ~comparador_de_mag_1_out_11);  // AND_Gate
  and and_8 (and_8_out, in_4, ~comparador_de_mag_1_out_11);  // AND_Gate
  or or_1 (MSB, and_1_out, and_8_out);
  or or_2 (out_6, and_2_out, and_7_out);
  or or_3 (out_7, and_3_out, and_6_out);
  or or_4 (LSB, and_4_out, and_5_out);
endmodule

module meio_somador (
  input  A,
  input  B,
  output co,
  output s
);

  and and_1 (co, A, B);
  xor xor_1 (s, B, A);
endmodule

module somador_completo (
  input  A,
  input  B,
  input  cin,
  output co,
  output s
);

  wire and_1_out, and_2_out, and_3_out, xor_1_out;

  and and_1 (and_1_out, A, B);
  and and_2 (and_2_out, A, cin);
  and and_3 (and_3_out, B, cin);
  xor xor_1 (xor_1_out, A, B);
  xor xor_2 (s, xor_1_out, cin);
  or or_1 (co, and_1_out, and_2_out, and_3_out);
endmodule

module comparador_de_mag (
  input  A0,
  input  B0,
  input  A1,
  input  B1,
  input  A2,
  input  B2,
  input  A3,
  input  B3,
  output out_9,
  output out_10,
  output out_11
);

  wire and_1_out, and_2_out, and_3_out, and_4_out, xnor_1_out, xnor_2_out, xnor_3_out, xnor_4_out;

  xnor xnor_1 (xnor_1_out, A0, B0);
  xnor xnor_2 (xnor_2_out, A1, B1);
  xnor xnor_3 (xnor_3_out, A2, B2);
  xnor xnor_4 (xnor_4_out, A3, B3);
  and and_1 (and_1_out, A0, ~B0, xnor_2_out, xnor_3_out, xnor_4_out);  // AND_Gate
  and and_2 (and_2_out, xnor_3_out, xnor_4_out, A1, ~B1);  // AND_Gate
  and and_3 (and_3_out, xnor_4_out, A2, ~B2);  // AND_Gate
  and and_4 (and_4_out, A3, ~B3);  // AND_Gate
  and and_5 (out_9, xnor_1_out, xnor_2_out, xnor_3_out, xnor_4_out);
  or or_1 (out_11, and_1_out, and_2_out, and_3_out, and_4_out);
  nor nor_1 (out_10, out_9, out_11);

  // Notes on the sheet:
  //   A = B
  //   A > B
  //   A < B
endmodule

module somador_4bits (
  input  MSB,
  input  in_2,
  input  LSB,
  input  in_4,
  input  MSB_2,
  input  in_6,
  input  LSB_2,
  input  in_8,
  input  in_9,
  output LSB_3,
  output out_11,
  output out_12,
  output MSB_3,
  output out_14
);

  wire meio_somador_1_co, meio_somador_1_s, somador_completo_1_co, somador_completo_1_s,
       somador_completo_2_co, somador_completo_2_s, somador_completo_3_s;

  meio_somador meio_somador_1 (.A(in_8), .B(in_4), .co(meio_somador_1_co), .s(meio_somador_1_s));
  somador_completo somador_completo_1 (
    .A(LSB_2), .B(LSB), .cin(meio_somador_1_co), .co(somador_completo_1_co), .s(somador_completo_1_s));
  somador_completo somador_completo_2 (
    .A(in_6), .B(in_2), .cin(somador_completo_1_co), .co(somador_completo_2_co), .s(somador_completo_2_s));
  somador_completo somador_completo_3 (
    .A(MSB_2), .B(MSB), .cin(somador_completo_2_co), .co(out_14), .s(somador_completo_3_s));
  and and_1 (LSB_3, meio_somador_1_s, in_9);
  and and_2 (out_11, somador_completo_1_s, in_9);
  and and_3 (out_12, somador_completo_2_s, in_9);
  and and_4 (MSB_3, somador_completo_3_s, in_9);

  // Notes on the sheet:
  //   B
  //   A
endmodule
