// Logisim project Maquina_de_estado_EXP.circ as structural Verilog: 3 circuits, main circuit main
module main (
);

  wire clock_1_out, \lógica_combinacional_1_n0 , \lógica_combinacional_1_n1 , \lógica_combinacional_1_w ,
       \lógica_combinacional_1_x , \lógica_combinacional_1_y , \lógica_combinacional_1_z ,
       registrador_de_estado_1_out_4, registrador_de_estado_1_out_5;

  Registrador_de_Estado registrador_de_estado_1 (
    .CLK(clock_1_out), .out_4(registrador_de_estado_1_out_4), .out_5(registrador_de_estado_1_out_5),
    .n0(\lógica_combinacional_1_n0 ), .n1(\lógica_combinacional_1_n1 ));
  Clock clock_1 (.out(clock_1_out));
  \Lógica_Combinacional  \lógica_combinacional_1  (
    .w(\lógica_combinacional_1_w ), .x(\lógica_combinacional_1_x ), .y(\lógica_combinacional_1_y ),
    .z(\lógica_combinacional_1_z ), .n1(\lógica_combinacional_1_n1 ), .n0(\lógica_combinacional_1_n0 ),
    .in_1(registrador_de_estado_1_out_5), .in_2(registrador_de_estado_1_out_4));
  LED led_1 (.in(\lógica_combinacional_1_w ));
  LED led_2 (.in(\lógica_combinacional_1_x ));
  LED led_3 (.in(\lógica_combinacional_1_y ));
  LED led_4 (.in(\lógica_combinacional_1_z ));

  // Notes on the sheet:
  //   Essa máquina de estado foi retirado do Livro do Vahid
  //   na página 140 do livro SIstemas Digitais: Projetos de Otimização e HDLs
endmodule

module Registrador_de_Estado (
  input  CLK,
  input  n0,
  input  n1,
  output out_4,
  output out_5
);

  D_Flip_Flop d_ff_1 (.clk(CLK), .D(n0), .Q(out_4));  // open: Qn, preset, en, reset
  D_Flip_Flop d_ff_2 (.clk(CLK), .D(n1), .Q(out_5));  // open: Qn, preset, en, reset
endmodule

module \Lógica_Combinacional  (
  input  in_1,
  input  in_2,
  output w,
  output x,
  output y,
  output z,
  output n1,
  output n0
);

  and and_1 (x, in_1, ~in_2);  // AND_Gate
  and and_2 (y, ~in_1, in_2);  // AND_Gate
  not not_1 (z, in_1);
  xor xor_1 (n1, in_1, in_2);
  not not_2 (n0, in_2);

  assign w = in_1;

  // Notes on the sheet:
  //   s1
  //   s0
endmodule
