// Logisim project Maquina_de_estado_EXP02.circ as structural Verilog: 4 circuits, main circuit main
module main (
  input  in_1,
  input  a,
  output [3:0] _1011
);

  wire clock_1_out, logica_combinacional_1_n0, logica_combinacional_1_n1, logica_combinacional_1_n2,
       logica_combinacional_1_r, registrado_de_estado_1_out_5, registrado_de_estado_1_out_6,
       registrado_de_estado_1_out_7;

  Registrado_de_estado registrado_de_estado_1 (
    .in_2(logica_combinacional_1_n0), .in_3(logica_combinacional_1_n1), .in_4(logica_combinacional_1_n2),
    .out_5(registrado_de_estado_1_out_5), .out_6(registrado_de_estado_1_out_6),
    .out_7(registrado_de_estado_1_out_7), .clk(clock_1_out));
  Clock clock_1 (.out(clock_1_out));
  Logica_Combinacional logica_combinacional_1 (
    .R(logica_combinacional_1_r), .n0(logica_combinacional_1_n0), .n1(logica_combinacional_1_n1),
    .n2(logica_combinacional_1_n2), .in_2(registrado_de_estado_1_out_7), .s1(registrado_de_estado_1_out_6),
    .s0(registrado_de_estado_1_out_5), .a(a));
  Registrador_Serial registrador_serial_1 (
    .CLK(clock_1_out), .Entrada(logica_combinacional_1_r), .Enable(in_1), .Y3(_1011[3]), .Y2(_1011[2]),
    .Y1(_1011[1]), .Y0(_1011[0]));

  // Notes on the sheet:
  //   CLK
  //   Este exemplo de máquna de estado foi retirado
  //   na página 141 do exemplo "Chave de carro segura"
  //   do livro de Vahid "Sistemas Digitais: Projetos de Otimização e HDLs
  //   O enable existe só por besteira mesmo, no exemplo não existe
  //   Valor que deve ter 
  //   ID
endmodule

module Registrado_de_estado (
  input  clk,
  input  in_2,
  input  in_3,
  input  in_4,
  output out_5,
  output out_6,
  output out_7
);

  D_Flip_Flop d_ff_1 (.clk(clk), .D(in_2), .Q(out_5));  // open: Qn, preset, en, reset
  D_Flip_Flop d_ff_2 (.clk(clk), .D(in_3), .Q(out_6));  // open: Qn, preset, en, reset
  D_Flip_Flop d_ff_3 (.clk(clk), .D(in_4), .Q(out_7));  // open: Qn, preset, en, reset

  // Notes on the sheet:
  //   n0
  //   s0
  //   n1
  //   s1
  //   n2
  //   s2
endmodule

module Registrador_Serial (
  input  CLK,
  input  Entrada,
  input  Enable,
  output Y3,
  output Y2,
  output Y1,
  output Y0
);

  D_Flip_Flop d_ff_1 (.clk(CLK), .D(Entrada), .Q(Y3), .en(Enable));  // open: Qn, preset, reset
  D_Flip_Flop d_ff_2 (.clk(CLK), .D(Y3), .Q(Y2), .en(Enable));  // open: Qn, preset, reset
  D_Flip_Flop d_ff_3 (.clk(CLK), .D(Y2), .Q(Y1), .en(Enable));  // open: Qn, preset, reset
  D_Flip_Flop d_ff_4 (.clk(CLK), .D(Y1), .Q(Y0), .en(Enable));  // open: Qn, preset, reset

  // Notes on the sheet:
  //   Ativa os FF's em 1
endmodule

module Logica_Combinacional (
  input  a,
  input  in_2,
  input  s1,
  input  s0,
  output R,
  output n0,
  output n1,
  output n2
);

  wire and_1_out, and_2_out, and_3_out, and_4_out, and_5_out, and_6_out;

  and and_1 (and_1_out, ~in_2, ~s1, s0);  // AND_Gate
  and and_2 (and_2_out, ~in_2, s1, ~s0);  // AND_Gate
  and and_3 (and_3_out, in_2, ~s1, ~s0);  // AND_Gate
  and and_4 (and_4_out, ~in_2, ~s1, ~s0, a);  // AND_Gate
  and and_5 (and_5_out, ~in_2, ~s1, s0);  // AND_Gate
  and and_6 (and_6_out, ~in_2, s1, ~s0);  // AND_Gate
  and and_7 (n2, ~in_2, s1, s0);  // AND_Gate
  or or_1 (n0, and_4_out, s1);
  or or_2 (n1, and_5_out, and_6_out);
  or or_3 (R, and_1_out, and_2_out, and_3_out, in_2);

  // Notes on the sheet:
  //   s2
endmodule
