// Logisim project Somador_Subtrator.circ as structural Verilog
module Somador_completo (
  input  A,
  input  B,
  input  cin,
  output co,
  output s
);

  wire and_1_out, and_2_out, and_3_out, xor_1_out;

  and and_1 (and_1_out, A, B);
  and and_2 (and_2_out, A, cin);
  and and_3 (and_3_out, B, cin);
  xor xor_1 (xor_1_out, A, B);
  xor xor_2 (s, xor_1_out, cin);
  or or_1 (co, and_1_out, and_2_out, and_3_out);
endmodule

module Subtrator_completo (
  input  A,
  input  B,
  input  Te,
  output To,
  output s
);

  wire and_1_out, and_2_out, and_3_out, xor_1_out;

  and and_1 (and_1_out, ~A, B);  // AND_Gate
  and and_2 (and_2_out, ~A, Te);  // AND_Gate
  and and_3 (and_3_out, B, Te);
  xor xor_1 (xor_1_out, A, B);
  xor xor_2 (s, xor_1_out, Te);
  or or_1 (To, and_1_out, and_2_out, and_3_out);
endmodule

module Meio_somador (
  input  A,
  input  B,
  output Co,
  output S
);

  and and_1 (Co, A, B);
  xor xor_1 (S, A, B);
endmodule

module Meio_subtrator (
  input  A,
  input  B,
  output To,
  output S
);

  and and_1 (To, ~A, B);  // AND_Gate
  xor xor_1 (S, A, B);
endmodule
